// Logisim project 16_bit_CPU.circ as structural Verilog
module ALU_INT (
  input  [15:0] IN_0,
  input  [15:0] IN_1,
  input  [2:0] SEL,
  input  SET,
  input  RST,
  output [15:0] OUT_0,
  output FLAG_ZERO,
  output FLAG_POS,
  output FLAG_NEG,
  output FLAG_OVF
);

  wire adder_1_cout, bitfinder_1_found, multiplexer_2_out, subtractor_1_bout;
  wire [2:0] register_3_q;
  wire [15:0] adder_1_out, and_1_out, multiplier_1_cout, multiplier_1_out, not_1_out, or_1_out, register_1_q,
       register_2_q, shifter_1_out, subtractor_1_out, xor_1_out;

  // Probe on IN_0
  // Probe on IN_1
  Register #(.width(16)) register_1 (.D(IN_0), .clk(SET), .Q(register_1_q), .clr(RST));  // open: en
  Register #(.width(16)) register_2 (.D(IN_1), .clk(SET), .Q(register_2_q), .clr(RST));  // open: en
  Register #(.width(3)) register_3 (.D(SEL), .clk(SET), .Q(register_3_q), .clr(RST));  // open: en
  Adder #(.width(16)) adder_1 (
    .a(register_1_q), .b(register_2_q), .out(adder_1_out), .cout(adder_1_cout));  // open: cin
  Multiplier #(.mode("twosComplement"), .width(16)) multiplier_1 (
    .a(register_1_q), .b(register_2_q), .out(multiplier_1_out), .cout(multiplier_1_cout));  // open: cin
  assign not_1_out = ~register_1_q;  // NOT_Gate not_1, 16 bits wide
  assign and_1_out = register_1_q & register_2_q;  // AND_Gate and_1, 16 bits wide
  assign or_1_out = register_1_q | register_2_q;  // OR_Gate or_1, 16 bits wide
  assign xor_1_out = register_1_q ^ register_2_q;  // XOR_Gate xor_1, 16 bits wide
  Subtractor #(.width(16)) subtractor_1 (
    .a(register_1_q), .b(register_2_q), .out(subtractor_1_out), .bout(subtractor_1_bout));  // open: bin
  Shifter #(.shift("rl"), .width(16)) shifter_1 (.in(register_1_q), .\dist (register_2_q[3:0]), .out(shifter_1_out));
  // Probe on OUT_0
  Multiplexer #(.select(3), .width(16)) multiplexer_1 (
    .in0(adder_1_out), .in1(subtractor_1_out), .in2(multiplier_1_out), .in3(shifter_1_out), .in4(not_1_out),
    .in5(and_1_out), .in6(or_1_out), .in7(xor_1_out), .out(OUT_0), .sel(register_3_q));
  BitFinder #(.width(16)) bitfinder_1 (.in(multiplier_1_cout), .found(bitfinder_1_found));  // open: index
  Comparator #(.width(16)) comparator_1 (.a(OUT_0), .b({16{1'b0}}), .gt(FLAG_POS), .eq(FLAG_ZERO), .lt(FLAG_NEG));
  Multiplexer #(.select(2)) multiplexer_2 (
    .in0(adder_1_cout), .in1(subtractor_1_bout), .in2(bitfinder_1_found), .in3(1'b0),
    .out(multiplexer_2_out), .sel(register_3_q[1:0]));
  and and_2 (FLAG_OVF, multiplexer_2_out, ~register_3_q[2]);  // AND_Gate
endmodule

module ALU_FLT (
  input  [31:0] IN_0,
  input  [31:0] IN_1,
  input  [2:0] SEL,
  input  SET,
  input  RST,
  output [31:0] OUT_0,
  output FLAG_ZERO,
  output FLAG_POS,
  output FLAG_NEG,
  output FLAG_ERR
);

  wire fptoint_1_p2, fptoint_1_p3, fptoint_1_p4, fptoint_1_p5, fptoint_1_p6, inttofp_1_p2;
  wire [2:0] register_3_q;
  wire [15:0] fptoint_1_p7;
  wire [31:0] fpadder_1_out, fpdivider_1_out, fpmultiplier_1_out, fpsubtractor_1_out, inttofp_1_p3,
       register_1_q, register_2_q;

  Register #(.width(32)) register_1 (.D(IN_0), .clk(SET), .Q(register_1_q), .clr(RST));  // open: en
  Register #(.width(32)) register_2 (.D(IN_1), .clk(SET), .Q(register_2_q), .clr(RST));  // open: en
  Register #(.width(3)) register_3 (.D(SEL), .clk(SET), .Q(register_3_q), .clr(RST));  // open: en
  FPAdder fpadder_1 (.a(register_1_q), .b(register_2_q), .out(fpadder_1_out));
  FPSubtractor fpsubtractor_1 (.a(register_1_q), .b(register_2_q), .out(fpsubtractor_1_out));
  FPMultiplier fpmultiplier_1 (.a(register_1_q), .b(register_2_q), .out(fpmultiplier_1_out));
  FPDivider fpdivider_1 (.a(register_1_q), .b(register_2_q), .out(fpdivider_1_out));
  // FPToInt #(.mode("truncate"), .width(16)) fptoint_1: pin names not known; wires that end beside it: register_1_q, fptoint_1_p2, fptoint_1_p3, fptoint_1_p4, fptoint_1_p5, fptoint_1_p6, fptoint_1_p7
  // IntToFP #(.width(16)) inttofp_1: pin names not known; wires that end beside it: register_1_q[15:0], inttofp_1_p2, inttofp_1_p3
  Multiplexer #(.select(3), .width(32)) multiplexer_1 (
    .in0(fpadder_1_out), .in1(fpsubtractor_1_out), .in2(fpmultiplier_1_out), .in3(fpdivider_1_out),
    .in4({{16{1'b0}}, fptoint_1_p7}), .in5(inttofp_1_p3), .out(OUT_0), .sel(register_3_q));  // open: in6, in7
  Multiplexer #(.select(3)) multiplexer_2 (
    .in0(fptoint_1_p2), .in1(fptoint_1_p3), .in2(fptoint_1_p4), .in3(fptoint_1_p5), .in4(fptoint_1_p6),
    .in5(inttofp_1_p2), .out(FLAG_ERR), .sel(register_3_q));  // open: in6, in7
  // FPComparator fpcomparator_1: pin names not known; wires that end beside it: OUT_0, {32{1'b0}}, FLAG_POS, FLAG_ZERO, FLAG_NEG
endmodule

module MAIN_CTR (
  input  CLK,
  input  [15:0] JMP_ADDR,
  input  JMP_SET,
  input  RST,
  output [15:0] CTR_OUT
);

  wire buffer_1_out, buffer_2_out;
  wire [15:0] adder_1_out, multiplexer_1_out;

  buf buffer_1 (buffer_1_out, CLK);
  buf buffer_2 (buffer_2_out, buffer_1_out);
  Multiplexer #(.width(16)) multiplexer_1 (.in0(adder_1_out), .in1(JMP_ADDR), .out(multiplexer_1_out), .sel(JMP_SET));
  Register #(.width(16)) register_1 (.D(multiplexer_1_out), .clk(buffer_2_out), .Q(CTR_OUT), .clr(RST));  // open: en
  Adder #(.width(16)) adder_1 (.a(CTR_OUT), .b(16'h1), .out(adder_1_out));  // open: cin, cout
endmodule

module CLK_MAIN (
  input  START,
  input  HALT,
  output CLK_OUT
);

  wire and_1_out, buffer_1_out, clock_1_out, not_1_out, or_1_out, s_r_ff_1_q;

  Clock clock_1 (.out(clock_1_out));
  buf buffer_1 (buffer_1_out, HALT);
  or or_1 (or_1_out, START, HALT);
  LED led_1 (.in(clock_1_out));
  S_R_Flip_Flop s_r_ff_1 (.S(START), .R(buffer_1_out), .clk(or_1_out), .Q(s_r_ff_1_q));  // open: reset, Qn, preset
  and and_1 (and_1_out, s_r_ff_1_q, clock_1_out);
  not not_1 (not_1_out, and_1_out);
  and and_2 (CLK_OUT, and_1_out, not_1_out);
endmodule

module PRGM_MEM (
  input  CLK_FETCH,
  input  [15:0] JUMP_ADDR,
  input  JUMP_SET,
  input  IO_MODE,
  input  [15:0] IO_ADDR,
  input  [15:0] SET_VAL,
  input  SET_TRIG,
  input  RST,
  output [15:0] INSTRUCTION,
  output [15:0] NEXT_BYTE,
  output CLK_OUT,
  output [15:0] IO_OUT
);

  wire and_1_out, and_2_out, buffer_1_out, buffer_2_out, buffer_3_out, buffer_4_out, buffer_5_out,
       buffer_6_out, buffer_7_out, buffer_8_out, buffer_9_out, buffer_10_out, buffer_11_out, buffer_12_out,
       buffer_13_out, buffer_14_out, buffer_15_out, buffer_16_out, buffer_17_out, buffer_18_out,
       buffer_19_out, buffer_20_out, buffer_21_out, buffer_22_out, buffer_23_out, buffer_24_out,
       buffer_25_out, buffer_26_out, buffer_27_out, buffer_28_out, buffer_29_out, buffer_30_out,
       buffer_31_out, buffer_32_out, buffer_33_out, buffer_34_out, buffer_35_out, buffer_36_out,
       buffer_37_out, buffer_38_out, buffer_39_out, buffer_40_out, buffer_41_out, buffer_42_out,
       buffer_43_out, buffer_44_out, buffer_45_out, buffer_46_out, buffer_47_out, buffer_48_out,
       buffer_49_out, buffer_50_out, buffer_51_out, buffer_52_out, buffer_53_out, buffer_54_out,
       buffer_55_out, buffer_56_out, buffer_57_out, buffer_58_out, buffer_59_out, buffer_60_out,
       buffer_61_out, next_decoder_1_read_next, or_1_out, or_2_out;
  wire [15:0] demultiplexer_1_out0, demultiplexer_1_out1, main_ctr_1_ctr_out, multiplexer_1_out;

  buf buffer_1 (buffer_1_out, and_1_out);
  buf buffer_2 (buffer_2_out, buffer_1_out);
  buf buffer_3 (buffer_3_out, buffer_2_out);
  or or_1 (or_1_out, buffer_3_out, JUMP_SET, CLK_FETCH);
  or or_2 (or_2_out, buffer_3_out, CLK_FETCH, SET_TRIG);
  // Probe on main_ctr_1_ctr_out
  MAIN_CTR main_ctr_1 (
    .CLK(or_1_out), .JMP_ADDR(JUMP_ADDR), .JMP_SET(JUMP_SET), .RST(RST), .CTR_OUT(main_ctr_1_ctr_out));
  buf buffer_4 (buffer_4_out, CLK_FETCH);
  buf buffer_5 (buffer_5_out, buffer_4_out);
  buf buffer_6 (buffer_6_out, buffer_5_out);
  buf buffer_7 (buffer_7_out, buffer_6_out);
  RAM #(.addrWidth(16), .dataWidth(16), .\type ("nonvolatile")) ram_1 (
    .addr(multiplexer_1_out), .we(SET_TRIG), .clk(or_2_out), .din(SET_VAL), .dout(IO_OUT));  // open: oe
  Multiplexer #(.width(16)) multiplexer_1 (
    .in0(main_ctr_1_ctr_out), .in1(IO_ADDR), .out(multiplexer_1_out), .sel(IO_MODE));
  buf buffer_8 (buffer_8_out, buffer_7_out);
  buf buffer_9 (buffer_9_out, buffer_8_out);
  buf buffer_10 (buffer_10_out, buffer_9_out);
  buf buffer_11 (buffer_11_out, buffer_10_out);
  buf buffer_12 (buffer_12_out, buffer_11_out);
  buf buffer_13 (buffer_13_out, buffer_12_out);
  buf buffer_14 (buffer_14_out, buffer_13_out);
  buf buffer_15 (buffer_15_out, buffer_14_out);
  buf buffer_16 (buffer_16_out, buffer_15_out);
  buf buffer_17 (buffer_17_out, buffer_16_out);
  buf buffer_18 (buffer_18_out, buffer_17_out);
  // Probe on IO_OUT
  buf buffer_19 (buffer_19_out, buffer_18_out);
  Demultiplexer #(.width(16)) demultiplexer_1 (
    .out0(demultiplexer_1_out0), .out1(demultiplexer_1_out1), .in(IO_OUT), .sel(buffer_22_out));
  buf buffer_20 (buffer_20_out, buffer_22_out);
  buf buffer_21 (buffer_21_out, buffer_20_out);
  buf buffer_22 (buffer_22_out, buffer_23_out);
  buf buffer_23 (buffer_23_out, buffer_24_out);
  buf buffer_24 (buffer_24_out, buffer_35_out);
  buf buffer_25 (buffer_25_out, buffer_19_out);
  buf buffer_26 (buffer_26_out, buffer_25_out);
  buf buffer_27 (buffer_27_out, buffer_26_out);
  buf buffer_28 (buffer_28_out, buffer_27_out);
  Register #(.width(16)) register_1 (
    .D(demultiplexer_1_out0), .clk(buffer_18_out), .Q(INSTRUCTION), .clr(RST));  // open: en
  Register #(.width(16)) register_2 (
    .D(demultiplexer_1_out1), .clk(buffer_29_out), .Q(NEXT_BYTE), .clr(RST));  // open: en
  buf buffer_29 (buffer_29_out, buffer_21_out);
  buf buffer_30 (buffer_30_out, buffer_28_out);
  buf buffer_31 (buffer_31_out, buffer_30_out);
  buf buffer_32 (buffer_32_out, buffer_31_out);
  buf buffer_33 (buffer_33_out, buffer_32_out);
  buf buffer_34 (buffer_34_out, buffer_35_out);
  buf buffer_35 (buffer_35_out, buffer_36_out);
  buf buffer_36 (buffer_36_out, buffer_44_out);
  buf buffer_37 (buffer_37_out, buffer_33_out);
  buf buffer_38 (buffer_38_out, buffer_37_out);
  buf buffer_39 (buffer_39_out, buffer_38_out);
  buf buffer_40 (buffer_40_out, buffer_34_out);
  buf buffer_41 (buffer_41_out, buffer_40_out);
  buf buffer_42 (buffer_42_out, buffer_41_out);
  buf buffer_43 (buffer_43_out, buffer_42_out);
  buf buffer_44 (buffer_44_out, buffer_45_out);
  buf buffer_45 (buffer_45_out, buffer_46_out);
  buf buffer_46 (buffer_46_out, buffer_47_out);
  buf buffer_47 (buffer_47_out, buffer_52_out);
  buf buffer_48 (buffer_48_out, buffer_43_out);
  buf buffer_49 (buffer_49_out, buffer_48_out);
  buf buffer_50 (buffer_50_out, buffer_49_out);
  buf buffer_51 (buffer_51_out, buffer_50_out);
  buf buffer_52 (buffer_52_out, buffer_53_out);
  buf buffer_53 (buffer_53_out, buffer_54_out);
  buf buffer_54 (buffer_54_out, buffer_55_out);
  buf buffer_55 (buffer_55_out, buffer_59_out);
  NEXT_DECODER next_decoder_1 (.INSTRUCTION(INSTRUCTION), .READ_NEXT(next_decoder_1_read_next));
  buf buffer_56 (buffer_56_out, buffer_51_out);
  buf buffer_57 (buffer_57_out, buffer_56_out);
  buf buffer_58 (buffer_58_out, buffer_57_out);
  buf buffer_59 (buffer_59_out, buffer_60_out);
  buf buffer_60 (buffer_60_out, buffer_61_out);
  buf buffer_61 (buffer_61_out, and_1_out);
  and and_1 (and_1_out, next_decoder_1_read_next, buffer_39_out);
  and and_2 (and_2_out, ~next_decoder_1_read_next, buffer_39_out);  // AND_Gate
  or or_3 (CLK_OUT, buffer_58_out, and_2_out);
endmodule

module PULSE (
  input  PLUSE_IN,
  output PULSE_OUT
);

  wire not_1_out;

  not not_1 (not_1_out, PLUSE_IN);
  and and_1 (PULSE_OUT, not_1_out, PLUSE_IN);
endmodule

module NEXT_DECODER (
  input  [15:0] INSTRUCTION,
  output READ_NEXT
);

  wire and_1_out, and_2_out, and_3_out;

  and and_1 (and_1_out, INSTRUCTION[12], ~INSTRUCTION[13], ~INSTRUCTION[14], ~INSTRUCTION[15]);  // AND_Gate
  and and_2 (and_2_out, ~INSTRUCTION[15], INSTRUCTION[14], INSTRUCTION[13]);  // AND_Gate
  and and_3 (and_3_out, INSTRUCTION[15], ~INSTRUCTION[14], INSTRUCTION[13], ~INSTRUCTION[12]);  // AND_Gate
  or or_1 (READ_NEXT, and_1_out, and_3_out, and_2_out);
endmodule

module CPU (
  input  START,
  input  RST,
  input  [15:0] IN_0,
  input  [15:0] IN_1,
  input  [15:0] IN_2,
  input  [15:0] IN_3,
  output [15:0] OUT_0,
  output [15:0] OUT_1,
  output [15:0] OUT_2,
  output [15:0] OUT_3,
  output [3:0] OUT_CLKS
);

  wire alu_float_section_1_alu_set, alu_float_section_1_ef_set, alu_section_1_1_alu_set,
       alu_section_1_1_reg_set_trig, alu_section_2_1_alu_set, alu_section_2_1_reg_set_trig,
       clk_main_1_clk_out, demultiplexer_2_out0, demultiplexer_2_out1, demultiplexer_2_out2,
       demultiplexer_2_out3, demultiplexer_2_out4, demultiplexer_2_out6, demultiplexer_2_out7,
       demultiplexer_2_out9, demultiplexer_2_out10, flow_section_1_halt, gp_ram_1_set_trig,
       io_section_1_set_trig, literal_jump_section_1_jump_set, load_section_1_reg_clk,
       move_section_1_set_trig, or_1_out, or_6_out, or_8_out, prgm_mem_1_clk_out;
  wire [2:0] alu_float_section_1_op_out, alu_section_1_1_alu_op_sel, alu_section_2_1_alu_op, or_7_out;
  wire [3:0] alu_flt_1_flag_zero, alu_int_1_flag_zero, alu_section_1_1_reg_sel, alu_section_1_1_reg_sel_2,
       alu_section_1_1_reg_set_sel, alu_section_2_1_reg_out_sel, alu_section_2_1_reg_sel_out,
       gp_ram_1_reg_sel, gp_ram_1_reg_sel_2, gp_ram_1_set_sel, io_section_1_read_sel, io_section_1_reg_sel,
       load_section_1_reg_sel, move_section_1_sel_out, move_section_1_sel_set, or_2_out, or_3_out, or_4_out;
  wire [11:0] demultiplexer_1_out0, demultiplexer_1_out1, demultiplexer_1_out2, demultiplexer_1_out3,
       demultiplexer_1_out4, demultiplexer_1_out6, demultiplexer_1_out7, demultiplexer_1_out9,
       demultiplexer_1_out10;
  wire [15:0] alu_int_1_out_0, alu_section_1_1_alu_in_0, alu_section_1_1_alu_in_1,
       alu_section_1_1_reg_set_val, alu_section_2_1_alu_out_0, alu_section_2_1_alu_out_1,
       alu_section_2_1_reg_out_val, gp_ram_1_set_val, io_section_1_set_val, literal_jump_section_1_jump_addr,
       load_section_1_reg_val, move_section_1_set_val, or_5_out, or_9_out, or_10_out, prgm_mem_1_instruction,
       prgm_mem_1_next_byte, registers_1_sel_2_out, registers_1_sel_out;
  wire [31:0] alu_float_section_1_ef_val, alu_flt_1_out_0, registers_1_r_ab_out, registers_1_r_cd_out;

  or or_1 (or_1_out, flow_section_1_halt, RST);
  CLK_MAIN clk_main_1 (.START(START), .HALT(or_1_out), .CLK_OUT(clk_main_1_clk_out));
  PRGM_MEM prgm_mem_1 (
    .CLK_FETCH(clk_main_1_clk_out), .JUMP_ADDR(literal_jump_section_1_jump_addr),
    .JUMP_SET(literal_jump_section_1_jump_set), .RST(RST), .INSTRUCTION(prgm_mem_1_instruction),
    .NEXT_BYTE(prgm_mem_1_next_byte), .CLK_OUT(prgm_mem_1_clk_out));  // open: IO_MODE, IO_ADDR, SET_VAL, SET_TRIG, IO_OUT
  Demultiplexer #(.select(4), .width(12)) demultiplexer_1 (
    .out0(demultiplexer_1_out0), .out1(demultiplexer_1_out1), .out2(demultiplexer_1_out2),
    .out3(demultiplexer_1_out3), .out4(demultiplexer_1_out4), .out6(demultiplexer_1_out6),
    .out7(demultiplexer_1_out7), .out9(demultiplexer_1_out9), .out10(demultiplexer_1_out10),
    .in(prgm_mem_1_instruction[11:0]), .sel(prgm_mem_1_instruction[15:12]));  // open: out5, out8, out11, out12, out13, out14, out15
  Demultiplexer #(.select(4)) demultiplexer_2 (
    .out0(demultiplexer_2_out0), .out1(demultiplexer_2_out1), .out2(demultiplexer_2_out2),
    .out3(demultiplexer_2_out3), .out4(demultiplexer_2_out4), .out6(demultiplexer_2_out6),
    .out7(demultiplexer_2_out7), .out9(demultiplexer_2_out9), .out10(demultiplexer_2_out10),
    .in(prgm_mem_1_clk_out), .sel(prgm_mem_1_instruction[15:12]));  // open: out5, out8, out11, out12, out13, out14, out15
  FLOW_SECTION flow_section_1 (.INSTR(demultiplexer_1_out0), .CLK(demultiplexer_2_out0), .HALT(flow_section_1_halt));
  LOAD_SECTION load_section_1 (
    .INSTRUCTION(demultiplexer_1_out1), .CLK(demultiplexer_2_out1), .NEXT_BYTE(prgm_mem_1_next_byte),
    .REG_SEL(load_section_1_reg_sel), .REG_CLK(load_section_1_reg_clk), .REG_VAL(load_section_1_reg_val));
  MOVE_SECTION move_section_1 (
    .INSTRUCTION(demultiplexer_1_out2), .CLK(demultiplexer_2_out2), .REG_IN(registers_1_sel_out),
    .SEL_OUT(move_section_1_sel_out), .SEL_SET(move_section_1_sel_set), .SET_VAL(move_section_1_set_val),
    .SET_TRIG(move_section_1_set_trig));
  IO_SECTION io_section_1 (
    .INSTRUTION(demultiplexer_1_out3), .CLK(demultiplexer_2_out3), .IN_0(IN_0), .IN_1(IN_1), .IN_2(IN_2),
    .IN_3(IN_3), .REG_IN(registers_1_sel_out), .RST(RST), .REG_SEL(io_section_1_reg_sel),
    .SET_TRIG(io_section_1_set_trig), .SET_VAL(io_section_1_set_val), .READ_SEL(io_section_1_read_sel),
    .OUT_0(OUT_0), .OUT_1(OUT_1), .OUT_2(OUT_2), .OUT_3(OUT_3), .OUT_CLKS(OUT_CLKS));
  GP_RAM gp_ram_1 (
    .INSTRUCTION(demultiplexer_1_out4), .CLK(demultiplexer_2_out4), .REG_IN(registers_1_sel_out),
    .REG_IN_2(registers_1_sel_2_out), .REG_SEL(gp_ram_1_reg_sel), .REG_SEL_2(gp_ram_1_reg_sel_2),
    .SET_SEL(gp_ram_1_set_sel), .SET_TRIG(gp_ram_1_set_trig), .SET_VAL(gp_ram_1_set_val));
  ALU_SECTION_1 alu_section_1_1 (
    .INSTRUCTION(demultiplexer_1_out6), .CLK(demultiplexer_2_out6), .NEXT_BYTE(prgm_mem_1_next_byte),
    .REG_IN(registers_1_sel_out), .REG_IN_2(registers_1_sel_2_out), .ALU_IN(alu_int_1_out_0),
    .REG_SEL(alu_section_1_1_reg_sel), .REG_SEL_2(alu_section_1_1_reg_sel_2),
    .ALU_IN_0(alu_section_1_1_alu_in_0), .ALU_IN_1(alu_section_1_1_alu_in_1),
    .ALU_OP_SEL(alu_section_1_1_alu_op_sel), .ALU_SET(alu_section_1_1_alu_set),
    .REG_SET_SEL(alu_section_1_1_reg_set_sel), .REG_SET_VAL(alu_section_1_1_reg_set_val),
    .REG_SET_TRIG(alu_section_1_1_reg_set_trig));
  ALU_SECTION_2 alu_section_2_1 (
    .INSTRUCTION(demultiplexer_1_out7), .CLK(demultiplexer_2_out7), .NEXT_BYTE(prgm_mem_1_next_byte),
    .REG_IN(registers_1_sel_out), .ALU_IN(alu_int_1_out_0), .REG_SEL_OUT(alu_section_2_1_reg_sel_out),
    .ALU_OUT_0(alu_section_2_1_alu_out_0), .ALU_OUT_1(alu_section_2_1_alu_out_1),
    .ALU_OP(alu_section_2_1_alu_op), .ALU_SET(alu_section_2_1_alu_set),
    .REG_OUT_SEL(alu_section_2_1_reg_out_sel), .REG_OUT_VAL(alu_section_2_1_reg_out_val),
    .REG_SET_TRIG(alu_section_2_1_reg_set_trig));
  ALU_FLOAT_SECTION alu_float_section_1 (
    .INSTRUCTION(demultiplexer_1_out9), .CLK(demultiplexer_2_out9), .ALU_IN(alu_flt_1_out_0),
    .OP_OUT(alu_float_section_1_op_out), .ALU_SET(alu_float_section_1_alu_set),
    .EF_VAL(alu_float_section_1_ef_val), .EF_SET(alu_float_section_1_ef_set));
  LITERAL_JUMP_SECTION literal_jump_section_1 (
    .INSTRUCTION(demultiplexer_1_out10), .CLK(demultiplexer_2_out10), .NEXT_BYTE(prgm_mem_1_next_byte),
    .CONDITIONS({alu_flt_1_flag_zero, alu_int_1_flag_zero}), .JUMP_ADDR(literal_jump_section_1_jump_addr),
    .JUMP_SET(literal_jump_section_1_jump_set));
  assign or_2_out = alu_section_1_1_reg_sel_2 | gp_ram_1_reg_sel_2;  // OR_Gate or_2, 4 bits wide
  assign or_3_out = alu_section_2_1_reg_sel_out | alu_section_1_1_reg_sel | gp_ram_1_reg_sel | io_section_1_read_sel | move_section_1_sel_out;  // OR_Gate or_3, 4 bits wide
  assign or_4_out = load_section_1_reg_sel | move_section_1_sel_set | io_section_1_reg_sel | gp_ram_1_set_sel | alu_section_1_1_reg_set_sel | alu_section_2_1_reg_out_sel;  // OR_Gate or_4, 4 bits wide
  assign or_5_out = load_section_1_reg_val | move_section_1_set_val | io_section_1_set_val | gp_ram_1_set_val | alu_section_1_1_reg_set_val | alu_section_2_1_reg_out_val;  // OR_Gate or_5, 16 bits wide
  or or_6 (or_6_out, load_section_1_reg_clk, move_section_1_set_trig, io_section_1_set_trig, gp_ram_1_set_trig, alu_section_1_1_reg_set_trig, alu_section_2_1_reg_set_trig);
  assign or_7_out = alu_section_1_1_alu_op_sel | alu_section_2_1_alu_op;  // OR_Gate or_7, 3 bits wide
  or or_8 (or_8_out, alu_section_1_1_alu_set, alu_section_2_1_alu_set);
  assign or_9_out = alu_section_1_1_alu_in_0 | alu_section_2_1_alu_out_0;  // OR_Gate or_9, 16 bits wide
  assign or_10_out = alu_section_1_1_alu_in_1 | alu_section_2_1_alu_out_1;  // OR_Gate or_10, 16 bits wide
  REGISTERS registers_1 (
    .RST(RST), .SET_VAL(or_5_out), .SET_TRIG(or_6_out), .SET_SEL(or_4_out), .OUT_SEL(or_3_out),
    .OUT_SEL_2(or_2_out), .R_EF_VAL(alu_float_section_1_ef_val), .R_EF_SET(alu_float_section_1_ef_set),
    .R_AB_OUT(registers_1_r_ab_out), .R_CD_OUT(registers_1_r_cd_out), .SEL_OUT(registers_1_sel_out),
    .SEL_2_OUT(registers_1_sel_2_out));
  ALU_INT alu_int_1 (
    .IN_0(or_9_out), .IN_1(or_10_out), .SEL(or_7_out), .SET(or_8_out), .RST(RST), .OUT_0(alu_int_1_out_0),
    .FLAG_ZERO(alu_int_1_flag_zero[0]), .FLAG_POS(alu_int_1_flag_zero[1]), .FLAG_NEG(alu_int_1_flag_zero[2]),
    .FLAG_OVF(alu_int_1_flag_zero[3]));
  ALU_FLT alu_flt_1 (
    .IN_0(registers_1_r_ab_out), .IN_1(registers_1_r_cd_out), .SEL(alu_float_section_1_op_out),
    .SET(alu_float_section_1_alu_set), .RST(RST), .OUT_0(alu_flt_1_out_0),
    .FLAG_ZERO(alu_flt_1_flag_zero[0]), .FLAG_POS(alu_flt_1_flag_zero[1]), .FLAG_NEG(alu_flt_1_flag_zero[2]),
    .FLAG_ERR(alu_flt_1_flag_zero[3]));
endmodule

module REGISTERS (
  input  [3:0] OUT_SEL,
  input  [3:0] OUT_SEL_2,
  input  [3:0] SET_SEL,
  input  [15:0] SET_VAL,
  input  SET_TRIG,
  input  RST,
  input  [31:0] R_EF_VAL,
  input  R_EF_SET,
  output [15:0] SEL_OUT,
  output [15:0] SEL_2_OUT,
  output [31:0] R_AB_OUT,
  output [31:0] R_CD_OUT
);

  wire demultiplexer_1_out0, demultiplexer_1_out1, demultiplexer_1_out2, demultiplexer_1_out3,
       demultiplexer_1_out4, demultiplexer_1_out5, demultiplexer_1_out6, demultiplexer_1_out7,
       demultiplexer_1_out8, demultiplexer_1_out9, demultiplexer_1_out10, demultiplexer_1_out11,
       demultiplexer_1_out12, demultiplexer_1_out13, demultiplexer_1_out14, demultiplexer_1_out15, or_1_out,
       or_2_out;
  wire [15:0] demultiplexer_2_out0, demultiplexer_2_out1, demultiplexer_2_out2, demultiplexer_2_out3,
       demultiplexer_2_out4, demultiplexer_2_out5, demultiplexer_2_out6, demultiplexer_2_out7,
       demultiplexer_2_out8, demultiplexer_2_out9, demultiplexer_2_out10, demultiplexer_2_out11,
       demultiplexer_2_out12, demultiplexer_2_out13, demultiplexer_2_out14, demultiplexer_2_out15, or_3_out,
       or_4_out, R_0_q, R_1_q, R_2_q, R_3_q, R_4_q, R_5_q, R_6_q, R_7_q, R_8_q, R_9_q, R_E_q, R_F_q;

  Demultiplexer #(.select(4)) demultiplexer_1 (
    .out0(demultiplexer_1_out0), .out1(demultiplexer_1_out1), .out2(demultiplexer_1_out2),
    .out3(demultiplexer_1_out3), .out4(demultiplexer_1_out4), .out5(demultiplexer_1_out5),
    .out6(demultiplexer_1_out6), .out7(demultiplexer_1_out7), .out8(demultiplexer_1_out8),
    .out9(demultiplexer_1_out9), .out10(demultiplexer_1_out10), .out11(demultiplexer_1_out11),
    .out12(demultiplexer_1_out12), .out13(demultiplexer_1_out13), .out14(demultiplexer_1_out14),
    .out15(demultiplexer_1_out15), .in(SET_TRIG), .sel(SET_SEL));
  Demultiplexer #(.select(4), .width(16)) demultiplexer_2 (
    .out0(demultiplexer_2_out0), .out1(demultiplexer_2_out1), .out2(demultiplexer_2_out2),
    .out3(demultiplexer_2_out3), .out4(demultiplexer_2_out4), .out5(demultiplexer_2_out5),
    .out6(demultiplexer_2_out6), .out7(demultiplexer_2_out7), .out8(demultiplexer_2_out8),
    .out9(demultiplexer_2_out9), .out10(demultiplexer_2_out10), .out11(demultiplexer_2_out11),
    .out12(demultiplexer_2_out12), .out13(demultiplexer_2_out13), .out14(demultiplexer_2_out14),
    .out15(demultiplexer_2_out15), .in(SET_VAL), .sel(SET_SEL));
  or or_1 (or_1_out, demultiplexer_1_out14, R_EF_SET);
  or or_2 (or_2_out, demultiplexer_1_out15, R_EF_SET);
  Register #(.width(16)) R_0 (.D(demultiplexer_2_out0), .clk(demultiplexer_1_out0), .Q(R_0_q), .clr(RST));  // open: en
  Register #(.width(16)) R_1 (.D(demultiplexer_2_out1), .clk(demultiplexer_1_out1), .Q(R_1_q), .clr(RST));  // open: en
  Register #(.width(16)) R_2 (.D(demultiplexer_2_out2), .clk(demultiplexer_1_out2), .Q(R_2_q), .clr(RST));  // open: en
  Register #(.width(16)) R_3 (.D(demultiplexer_2_out3), .clk(demultiplexer_1_out3), .Q(R_3_q), .clr(RST));  // open: en
  Register #(.width(16)) R_4 (.D(demultiplexer_2_out4), .clk(demultiplexer_1_out4), .Q(R_4_q), .clr(RST));  // open: en
  Register #(.width(16)) R_5 (.D(demultiplexer_2_out5), .clk(demultiplexer_1_out5), .Q(R_5_q), .clr(RST));  // open: en
  Register #(.width(16)) R_6 (.D(demultiplexer_2_out6), .clk(demultiplexer_1_out6), .Q(R_6_q), .clr(RST));  // open: en
  Register #(.width(16)) R_7 (.D(demultiplexer_2_out7), .clk(demultiplexer_1_out7), .Q(R_7_q), .clr(RST));  // open: en
  Register #(.width(16)) R_8 (.D(demultiplexer_2_out8), .clk(demultiplexer_1_out8), .Q(R_8_q), .clr(RST));  // open: en
  Register #(.width(16)) R_9 (.D(demultiplexer_2_out9), .clk(demultiplexer_1_out9), .Q(R_9_q), .clr(RST));  // open: en
  Register #(.width(16)) R_A (
    .D(demultiplexer_2_out10), .clk(demultiplexer_1_out10), .Q(R_AB_OUT[15:0]), .clr(RST));  // open: en
  Register #(.width(16)) R_B (
    .D(demultiplexer_2_out11), .clk(demultiplexer_1_out11), .Q(R_AB_OUT[31:16]), .clr(RST));  // open: en
  Register #(.width(16)) R_C (
    .D(demultiplexer_2_out12), .clk(demultiplexer_1_out12), .Q(R_CD_OUT[15:0]), .clr(RST));  // open: en
  Register #(.width(16)) R_D (
    .D(demultiplexer_2_out13), .clk(demultiplexer_1_out13), .Q(R_CD_OUT[31:16]), .clr(RST));  // open: en
  Register #(.width(16)) R_E (.D(or_3_out), .clk(or_1_out), .Q(R_E_q), .clr(RST));  // open: en
  assign or_3_out = demultiplexer_2_out14 | R_EF_VAL[15:0];  // OR_Gate or_3, 16 bits wide
  Register #(.width(16)) R_F (.D(or_4_out), .clk(or_2_out), .Q(R_F_q), .clr(RST));  // open: en
  assign or_4_out = demultiplexer_2_out15 | R_EF_VAL[31:16];  // OR_Gate or_4, 16 bits wide
  Multiplexer #(.select(4), .width(16)) multiplexer_1 (
    .in0(R_0_q), .in1(R_1_q), .in2(R_2_q), .in3(R_3_q), .in4(R_4_q), .in5(R_5_q), .in6(R_6_q), .in7(R_7_q),
    .in8(R_8_q), .in9(R_9_q), .in10(R_AB_OUT[15:0]), .in11(R_AB_OUT[31:16]), .in12(R_CD_OUT[15:0]),
    .in13(R_CD_OUT[31:16]), .in14(R_E_q), .in15(R_F_q), .out(SEL_OUT), .sel(OUT_SEL));
  Multiplexer #(.select(4), .width(16)) multiplexer_2 (
    .in0(R_0_q), .in1(R_1_q), .in2(R_2_q), .in3(R_3_q), .in4(R_4_q), .in5(R_5_q), .in6(R_6_q), .in7(R_7_q),
    .in8(R_8_q), .in9(R_9_q), .in10(R_AB_OUT[15:0]), .in11(R_AB_OUT[31:16]), .in12(R_CD_OUT[15:0]),
    .in13(R_CD_OUT[31:16]), .in14(R_E_q), .in15(R_F_q), .out(SEL_2_OUT), .sel(OUT_SEL_2));
endmodule

module FLOW_SECTION (
  input  [11:0] INSTR,
  input  CLK,
  output HALT
);

  and and_1 (HALT, INSTR[0], CLK);
endmodule

module LOAD_SECTION (
  input  [11:0] INSTRUCTION,
  input  CLK,
  input  [15:0] NEXT_BYTE,
  output [3:0] REG_SEL,
  output REG_CLK,
  output [15:0] REG_VAL
);

  wire buffer_1_out, buffer_2_out;

  Multiplexer #(.width(4)) multiplexer_1 (.in0(4'b0000), .in1(INSTRUCTION[3:0]), .out(REG_SEL), .sel(CLK));
  Multiplexer #(.width(16)) multiplexer_2 (.in0({16{1'b0}}), .in1(NEXT_BYTE), .out(REG_VAL), .sel(CLK));
  buf buffer_1 (buffer_1_out, CLK);
  buf buffer_2 (buffer_2_out, buffer_1_out);
  buf buffer_3 (REG_CLK, buffer_2_out);
endmodule

module MOVE_SECTION (
  input  [11:0] INSTRUCTION,
  input  CLK,
  input  [15:0] REG_IN,
  output [3:0] SEL_OUT,
  output [3:0] SEL_SET,
  output [15:0] SET_VAL,
  output SET_TRIG
);

  wire buffer_1_out, buffer_2_out, buffer_3_out, buffer_4_out, buffer_5_out, buffer_6_out, buffer_7_out,
       buffer_8_out, buffer_9_out, buffer_10_out, buffer_11_out, buffer_12_out, buffer_13_out, buffer_14_out,
       buffer_15_out, buffer_16_out;

  buf buffer_1 (buffer_1_out, CLK);
  buf buffer_2 (buffer_2_out, buffer_1_out);
  buf buffer_3 (buffer_3_out, buffer_7_out);
  buf buffer_4 (buffer_4_out, buffer_3_out);
  Multiplexer #(.width(4)) multiplexer_1 (.in0(4'b0000), .in1(INSTRUCTION[7:4]), .out(SEL_OUT), .sel(buffer_5_out));
  buf buffer_5 (buffer_5_out, buffer_2_out);
  buf buffer_6 (buffer_6_out, buffer_5_out);
  buf buffer_7 (buffer_7_out, buffer_8_out);
  buf buffer_8 (buffer_8_out, buffer_9_out);
  buf buffer_9 (buffer_9_out, buffer_6_out);
  buf buffer_10 (buffer_10_out, buffer_4_out);
  buf buffer_11 (buffer_11_out, buffer_10_out);
  buf buffer_12 (buffer_12_out, buffer_11_out);
  buf buffer_13 (buffer_13_out, buffer_12_out);
  Multiplexer #(.width(4)) multiplexer_2 (.in0(4'b0000), .in1(INSTRUCTION[3:0]), .out(SEL_SET), .sel(buffer_14_out));
  Multiplexer #(.width(16)) multiplexer_3 (.in0({16{1'b0}}), .in1(REG_IN), .out(SET_VAL), .sel(buffer_14_out));
  buf buffer_14 (buffer_14_out, buffer_13_out);
  buf buffer_15 (buffer_15_out, buffer_14_out);
  buf buffer_16 (buffer_16_out, buffer_15_out);
  buf buffer_17 (SET_TRIG, buffer_16_out);
endmodule

module IO_SECTION (
  input  [11:0] INSTRUTION,
  input  CLK,
  input  [15:0] IN_0,
  input  [15:0] IN_1,
  input  [15:0] IN_2,
  input  [15:0] IN_3,
  input  [15:0] REG_IN,
  input  RST,
  output [3:0] REG_SEL,
  output SET_TRIG,
  output [15:0] SET_VAL,
  output [3:0] READ_SEL,
  output [15:0] OUT_0,
  output [15:0] OUT_1,
  output [15:0] OUT_2,
  output [15:0] OUT_3,
  output [3:0] OUT_CLKS
);

  wire and_1_out, and_2_out, buffer_1_out, buffer_2_out, buffer_4_out, buffer_5_out, buffer_6_out,
       buffer_7_out, buffer_8_out, buffer_9_out, buffer_10_out, buffer_11_out, buffer_12_out, buffer_13_out,
       buffer_14_out, buffer_15_out, buffer_16_out, buffer_17_out, buffer_18_out, buffer_19_out,
       buffer_20_out, buffer_21_out, buffer_22_out, buffer_23_out, buffer_24_out, buffer_25_out,
       buffer_26_out, buffer_27_out, buffer_28_out, buffer_29_out, buffer_30_out, buffer_31_out,
       buffer_32_out, buffer_34_out, buffer_35_out, buffer_37_out, buffer_38_out, buffer_40_out,
       buffer_41_out, demultiplexer_2_out0, demultiplexer_2_out1, demultiplexer_2_out2, demultiplexer_2_out3;
  wire [15:0] demultiplexer_1_out0, demultiplexer_1_out1, demultiplexer_1_out2, demultiplexer_1_out3,
       multiplexer_1_out;

  and and_1 (and_1_out, ~INSTRUTION[10], CLK);  // AND_Gate
  and and_2 (and_2_out, INSTRUTION[10], CLK);
  Multiplexer #(.select(2), .width(16)) multiplexer_1 (
    .in0(IN_0), .in1(IN_1), .in2(IN_2), .in3(IN_3), .out(multiplexer_1_out), .sel(INSTRUTION[9:8]));
  Demultiplexer #(.select(2), .width(16)) demultiplexer_1 (
    .out0(demultiplexer_1_out0), .out1(demultiplexer_1_out1), .out2(demultiplexer_1_out2),
    .out3(demultiplexer_1_out3), .in(REG_IN), .sel(INSTRUTION[9:8]));
  Demultiplexer #(.select(2)) demultiplexer_2 (
    .out0(demultiplexer_2_out0), .out1(demultiplexer_2_out1), .out2(demultiplexer_2_out2),
    .out3(demultiplexer_2_out3), .in(buffer_30_out), .sel(INSTRUTION[9:8]));
  Multiplexer #(.width(4)) multiplexer_2 (.in0(4'b0000), .in1(INSTRUTION[3:0]), .out(REG_SEL), .sel(and_1_out));
  buf buffer_1 (buffer_1_out, and_1_out);
  buf buffer_2 (buffer_2_out, buffer_1_out);
  Multiplexer #(.width(16)) multiplexer_3 (.in0({16{1'b0}}), .in1(multiplexer_1_out), .out(SET_VAL), .sel(and_1_out));
  Multiplexer #(.width(4)) multiplexer_4 (.in0(4'b0000), .in1(INSTRUTION[3:0]), .out(READ_SEL), .sel(and_2_out));
  buf buffer_3 (SET_TRIG, buffer_2_out);
  Register #(.width(16)) register_1 (
    .D(demultiplexer_1_out0), .clk(demultiplexer_2_out0), .Q(OUT_0), .clr(RST));  // open: en
  Register #(.width(16)) register_2 (
    .D(demultiplexer_1_out1), .clk(demultiplexer_2_out1), .Q(OUT_1), .clr(RST));  // open: en
  Register #(.width(16)) register_3 (
    .D(demultiplexer_1_out2), .clk(demultiplexer_2_out2), .Q(OUT_2), .clr(RST));  // open: en
  Register #(.width(16)) register_4 (
    .D(demultiplexer_1_out3), .clk(demultiplexer_2_out3), .Q(OUT_3), .clr(RST));  // open: en
  buf buffer_4 (buffer_4_out, and_2_out);
  buf buffer_5 (buffer_5_out, buffer_4_out);
  buf buffer_6 (buffer_6_out, buffer_5_out);
  buf buffer_7 (buffer_7_out, buffer_6_out);
  buf buffer_8 (buffer_8_out, buffer_7_out);
  buf buffer_9 (buffer_9_out, buffer_8_out);
  buf buffer_10 (buffer_10_out, buffer_9_out);
  buf buffer_11 (buffer_11_out, buffer_10_out);
  buf buffer_12 (buffer_12_out, demultiplexer_2_out0);
  buf buffer_13 (buffer_13_out, buffer_12_out);
  buf buffer_14 (buffer_14_out, buffer_13_out);
  buf buffer_15 (buffer_15_out, buffer_14_out);
  buf buffer_16 (buffer_16_out, demultiplexer_2_out1);
  buf buffer_17 (buffer_17_out, buffer_16_out);
  buf buffer_18 (buffer_18_out, buffer_17_out);
  buf buffer_19 (buffer_19_out, buffer_18_out);
  buf buffer_20 (buffer_20_out, demultiplexer_2_out2);
  buf buffer_21 (buffer_21_out, buffer_20_out);
  buf buffer_22 (buffer_22_out, buffer_21_out);
  buf buffer_23 (buffer_23_out, buffer_22_out);
  buf buffer_24 (buffer_24_out, demultiplexer_2_out3);
  buf buffer_25 (buffer_25_out, buffer_24_out);
  buf buffer_26 (buffer_26_out, buffer_25_out);
  buf buffer_27 (buffer_27_out, buffer_26_out);
  buf buffer_28 (buffer_28_out, buffer_11_out);
  buf buffer_29 (buffer_29_out, buffer_28_out);
  buf buffer_30 (buffer_30_out, buffer_29_out);
  buf buffer_31 (buffer_31_out, buffer_15_out);
  buf buffer_32 (buffer_32_out, buffer_31_out);
  buf buffer_33 (OUT_CLKS[0], buffer_32_out);
  buf buffer_34 (buffer_34_out, buffer_19_out);
  buf buffer_35 (buffer_35_out, buffer_34_out);
  buf buffer_36 (OUT_CLKS[1], buffer_35_out);
  buf buffer_37 (buffer_37_out, buffer_23_out);
  buf buffer_38 (buffer_38_out, buffer_37_out);
  buf buffer_39 (OUT_CLKS[2], buffer_38_out);
  buf buffer_40 (buffer_40_out, buffer_27_out);
  buf buffer_41 (buffer_41_out, buffer_40_out);
  buf buffer_42 (OUT_CLKS[3], buffer_41_out);
endmodule

module GP_RAM (
  input  [11:0] INSTRUCTION,
  input  CLK,
  input  [15:0] REG_IN,
  input  [15:0] REG_IN_2,
  output [3:0] REG_SEL,
  output [3:0] REG_SEL_2,
  output [3:0] SET_SEL,
  output SET_TRIG,
  output [15:0] SET_VAL
);

  wire and_1_out, and_2_out, buffer_1_out, buffer_2_out, buffer_3_out, buffer_4_out, buffer_5_out,
       buffer_6_out, buffer_7_out, buffer_8_out, buffer_9_out, buffer_10_out, buffer_11_out, buffer_12_out,
       buffer_13_out, buffer_14_out, buffer_15_out, buffer_16_out, buffer_17_out, buffer_18_out,
       buffer_19_out, buffer_20_out, buffer_21_out, buffer_22_out, buffer_23_out, buffer_24_out,
       buffer_25_out, buffer_26_out, buffer_27_out, buffer_28_out, buffer_29_out, buffer_30_out,
       buffer_31_out, buffer_32_out, buffer_33_out, buffer_34_out, buffer_35_out, or_1_out, or_2_out;
  wire [15:0] ram_1_dout;

  and and_1 (and_1_out, ~INSTRUCTION[8], CLK);  // AND_Gate
  and and_2 (and_2_out, INSTRUCTION[8], CLK);
  buf buffer_1 (buffer_1_out, and_1_out);
  Multiplexer #(.width(4)) multiplexer_1 (.in0(4'b0000), .in1(INSTRUCTION[3:0]), .out(REG_SEL), .sel(and_1_out));
  Multiplexer #(.width(4)) multiplexer_2 (.in0(4'b0000), .in1(INSTRUCTION[7:4]), .out(REG_SEL_2), .sel(or_1_out));
  or or_1 (or_1_out, and_2_out, and_1_out);
  buf buffer_2 (buffer_2_out, buffer_1_out);
  buf buffer_3 (buffer_3_out, buffer_2_out);
  buf buffer_4 (buffer_4_out, buffer_3_out);
  buf buffer_5 (buffer_5_out, buffer_4_out);
  buf buffer_6 (buffer_6_out, buffer_19_out);
  or or_2 (or_2_out, buffer_19_out, buffer_22_out);
  buf buffer_7 (buffer_7_out, and_2_out);
  buf buffer_8 (buffer_8_out, buffer_7_out);
  buf buffer_9 (buffer_9_out, buffer_8_out);
  buf buffer_10 (buffer_10_out, buffer_9_out);
  buf buffer_11 (buffer_11_out, buffer_5_out);
  buf buffer_12 (buffer_12_out, buffer_11_out);
  buf buffer_13 (buffer_13_out, buffer_12_out);
  buf buffer_14 (buffer_14_out, buffer_13_out);
  RAM #(.addrWidth(16), .dataWidth(16), .\type ("nonvolatile")) ram_1 (
    .addr(REG_IN_2), .we(buffer_6_out), .clk(or_2_out), .din(REG_IN), .dout(ram_1_dout));  // open: oe
  buf buffer_15 (buffer_15_out, buffer_10_out);
  buf buffer_16 (buffer_16_out, buffer_15_out);
  buf buffer_17 (buffer_17_out, buffer_16_out);
  buf buffer_18 (buffer_18_out, buffer_17_out);
  buf buffer_19 (buffer_19_out, buffer_14_out);
  buf buffer_20 (buffer_20_out, buffer_18_out);
  buf buffer_21 (buffer_21_out, buffer_20_out);
  buf buffer_22 (buffer_22_out, buffer_21_out);
  buf buffer_23 (buffer_23_out, buffer_22_out);
  buf buffer_24 (buffer_24_out, buffer_23_out);
  buf buffer_25 (buffer_25_out, buffer_26_out);
  buf buffer_26 (buffer_26_out, buffer_27_out);
  buf buffer_27 (buffer_27_out, buffer_32_out);
  buf buffer_28 (buffer_28_out, buffer_25_out);
  buf buffer_29 (buffer_29_out, buffer_28_out);
  buf buffer_30 (buffer_30_out, buffer_24_out);
  buf buffer_31 (buffer_31_out, buffer_30_out);
  buf buffer_32 (buffer_32_out, buffer_31_out);
  buf buffer_33 (buffer_33_out, buffer_29_out);
  Multiplexer #(.width(4)) multiplexer_3 (.in0(4'b0000), .in1(INSTRUCTION[3:0]), .out(SET_SEL), .sel(buffer_33_out));
  buf buffer_34 (buffer_34_out, buffer_33_out);
  buf buffer_35 (buffer_35_out, buffer_34_out);
  buf buffer_36 (SET_TRIG, buffer_35_out);
  Multiplexer #(.width(16)) multiplexer_4 (.in0({16{1'b0}}), .in1(ram_1_dout), .out(SET_VAL), .sel(buffer_33_out));
endmodule

module ALU_SECTION_1 (
  input  [11:0] INSTRUCTION,
  input  CLK,
  input  [15:0] NEXT_BYTE,
  input  [15:0] REG_IN,
  input  [15:0] REG_IN_2,
  input  [15:0] ALU_IN,
  output [3:0] REG_SEL,
  output [3:0] REG_SEL_2,
  output [15:0] ALU_IN_0,
  output [15:0] ALU_IN_1,
  output [2:0] ALU_OP_SEL,
  output ALU_SET,
  output [3:0] REG_SET_SEL,
  output [15:0] REG_SET_VAL,
  output REG_SET_TRIG
);

  wire and_1_out, and_2_out, and_3_out, buffer_1_out, buffer_2_out, buffer_3_out, buffer_4_out, buffer_5_out,
       buffer_6_out, buffer_7_out, buffer_8_out, buffer_9_out, buffer_10_out, buffer_11_out, buffer_12_out,
       buffer_13_out, buffer_14_out, buffer_15_out, buffer_16_out, buffer_17_out, buffer_18_out,
       buffer_19_out, buffer_21_out, buffer_22_out, buffer_24_out, buffer_25_out, buffer_26_out,
       buffer_27_out, buffer_28_out, buffer_29_out, buffer_30_out, buffer_31_out, buffer_32_out,
       buffer_33_out, buffer_34_out, buffer_35_out, buffer_36_out, buffer_37_out, buffer_38_out,
       buffer_39_out, buffer_40_out, buffer_41_out, buffer_42_out, buffer_43_out, buffer_44_out,
       buffer_45_out, buffer_46_out, buffer_47_out, buffer_48_out, buffer_49_out, buffer_50_out,
       buffer_51_out, buffer_52_out, buffer_53_out, buffer_54_out, buffer_55_out, buffer_56_out,
       buffer_57_out, buffer_58_out, buffer_59_out, buffer_60_out, buffer_61_out, buffer_62_out,
       buffer_63_out, buffer_64_out, buffer_65_out, buffer_66_out, buffer_67_out, buffer_68_out,
       buffer_69_out, buffer_70_out, buffer_71_out, buffer_72_out, buffer_73_out, buffer_74_out,
       buffer_75_out, buffer_76_out, buffer_77_out, buffer_78_out, buffer_79_out, buffer_80_out,
       buffer_81_out, buffer_82_out, buffer_83_out, buffer_84_out, buffer_85_out, buffer_86_out,
       buffer_87_out, buffer_88_out, buffer_89_out, buffer_90_out, buffer_91_out, buffer_92_out,
       buffer_93_out, buffer_94_out, buffer_95_out, buffer_96_out, buffer_97_out, buffer_98_out,
       buffer_99_out, buffer_100_out, buffer_101_out, buffer_102_out, buffer_103_out, buffer_104_out,
       buffer_105_out, buffer_106_out, buffer_107_out, buffer_108_out, buffer_109_out, buffer_110_out,
       buffer_111_out, buffer_112_out, buffer_113_out, buffer_114_out, buffer_115_out, buffer_116_out,
       buffer_117_out, buffer_118_out, buffer_119_out, buffer_120_out, buffer_121_out, buffer_122_out,
       buffer_123_out, buffer_124_out, buffer_125_out, buffer_126_out, buffer_127_out, buffer_128_out,
       buffer_129_out, buffer_130_out, buffer_131_out, buffer_132_out, buffer_133_out, buffer_134_out,
       buffer_135_out, buffer_136_out, buffer_137_out, buffer_138_out, buffer_139_out, buffer_140_out,
       buffer_141_out, buffer_142_out, buffer_143_out, buffer_144_out, buffer_145_out, buffer_146_out,
       buffer_147_out, buffer_148_out, buffer_149_out, buffer_150_out, buffer_151_out, buffer_152_out,
       buffer_153_out, buffer_154_out, buffer_155_out, buffer_156_out, buffer_157_out, buffer_158_out,
       buffer_159_out, buffer_160_out, buffer_161_out, buffer_162_out, buffer_163_out, buffer_164_out,
       buffer_165_out, buffer_166_out, buffer_167_out, buffer_168_out, buffer_169_out, buffer_170_out,
       buffer_171_out, buffer_172_out, buffer_173_out, buffer_174_out, buffer_175_out, buffer_176_out,
       buffer_177_out, buffer_178_out, buffer_179_out, buffer_180_out, buffer_181_out, buffer_182_out,
       buffer_183_out, buffer_184_out, buffer_185_out, buffer_186_out, buffer_187_out, buffer_188_out,
       buffer_189_out, buffer_190_out, buffer_191_out, buffer_192_out, buffer_193_out, buffer_194_out,
       buffer_195_out, buffer_196_out, buffer_197_out, buffer_198_out, buffer_199_out, buffer_200_out,
       buffer_201_out, buffer_202_out, buffer_203_out, buffer_204_out, buffer_205_out, buffer_206_out,
       buffer_207_out, buffer_208_out, buffer_209_out, buffer_210_out, buffer_211_out, buffer_212_out,
       buffer_213_out, buffer_214_out, buffer_215_out, buffer_216_out, buffer_217_out, buffer_218_out,
       buffer_219_out, buffer_220_out, buffer_221_out, buffer_222_out, buffer_223_out, buffer_224_out,
       buffer_225_out, buffer_226_out, buffer_227_out, buffer_228_out, buffer_229_out, buffer_230_out,
       buffer_231_out, buffer_232_out, buffer_233_out, buffer_234_out, buffer_235_out, buffer_236_out,
       buffer_237_out, buffer_238_out, buffer_239_out, buffer_240_out, buffer_241_out, buffer_242_out,
       buffer_243_out, buffer_244_out, buffer_245_out, buffer_246_out, buffer_247_out, buffer_248_out,
       buffer_249_out, buffer_250_out, buffer_251_out, buffer_252_out, buffer_253_out, buffer_254_out,
       buffer_255_out, buffer_256_out, buffer_257_out, buffer_258_out, buffer_259_out, buffer_260_out,
       buffer_261_out, buffer_262_out, buffer_263_out, buffer_264_out, buffer_265_out, buffer_266_out,
       buffer_267_out, buffer_268_out, buffer_269_out, buffer_270_out, buffer_271_out, buffer_272_out,
       buffer_273_out, buffer_274_out, buffer_275_out, buffer_276_out, buffer_277_out, buffer_278_out,
       buffer_279_out, buffer_280_out, buffer_281_out, buffer_282_out, buffer_283_out, buffer_284_out,
       buffer_285_out, buffer_286_out, buffer_287_out, buffer_288_out, buffer_289_out, buffer_290_out,
       buffer_291_out, buffer_292_out, buffer_293_out, buffer_294_out, buffer_295_out, buffer_296_out,
       buffer_297_out, buffer_298_out, buffer_299_out, buffer_300_out, buffer_301_out, buffer_302_out,
       buffer_303_out, buffer_304_out, buffer_305_out, buffer_306_out, buffer_307_out, buffer_308_out,
       buffer_309_out, buffer_310_out, buffer_311_out, buffer_312_out, buffer_313_out, buffer_314_out,
       buffer_315_out, buffer_316_out, buffer_317_out, buffer_318_out, buffer_319_out, buffer_320_out,
       buffer_321_out, buffer_322_out, buffer_323_out, buffer_324_out, buffer_325_out, buffer_326_out,
       buffer_327_out, buffer_328_out, buffer_329_out, buffer_330_out, buffer_331_out, buffer_332_out,
       buffer_333_out, buffer_334_out, buffer_335_out, buffer_336_out, buffer_337_out, buffer_338_out,
       buffer_339_out, buffer_340_out, or_1_out;
  wire [2:0] xnor_1_out;

  buf buffer_1 (buffer_1_out, CLK);
  buf buffer_2 (buffer_2_out, buffer_1_out);
  buf buffer_3 (buffer_3_out, buffer_2_out);
  buf buffer_4 (buffer_4_out, buffer_3_out);
  buf buffer_5 (buffer_5_out, buffer_4_out);
  buf buffer_6 (buffer_6_out, buffer_5_out);
  buf buffer_7 (buffer_7_out, buffer_6_out);
  and and_1 (and_1_out, xnor_1_out[0], xnor_1_out[1], xnor_1_out[2]);
  Multiplexer #(.width(4)) multiplexer_1 (.in0(4'b0000), .in1(INSTRUCTION[3:0]), .out(REG_SEL), .sel(CLK));
  Multiplexer #(.width(4)) multiplexer_2 (.in0(4'b0000), .in1(NEXT_BYTE[3:0]), .out(REG_SEL_2), .sel(CLK));
  buf buffer_8 (buffer_8_out, buffer_7_out);
  buf buffer_9 (buffer_9_out, buffer_8_out);
  buf buffer_10 (buffer_10_out, buffer_9_out);
  buf buffer_11 (buffer_11_out, buffer_10_out);
  Multiplexer #(.width(16)) multiplexer_3 (.in0({16{1'b0}}), .in1(REG_IN), .out(ALU_IN_0), .sel(buffer_11_out));
  Multiplexer #(.width(16)) multiplexer_4 (.in0({16{1'b0}}), .in1(REG_IN_2), .out(ALU_IN_1), .sel(buffer_11_out));
  Multiplexer #(.width(3)) multiplexer_5 (.in0(3'b000), .in1(INSTRUCTION[10:8]), .out(ALU_OP_SEL), .sel(buffer_11_out));
  buf buffer_12 (buffer_12_out, buffer_11_out);
  buf buffer_13 (buffer_13_out, buffer_12_out);
  or or_1 (or_1_out, and_2_out, and_3_out);
  and and_2 (and_2_out, ~and_1_out, buffer_15_out);  // AND_Gate
  assign xnor_1_out = ~(INSTRUCTION[10:8] ^ 3'b010);  // XNOR_Gate xnor_1, 3 bits wide
  buf buffer_14 (buffer_14_out, buffer_15_out);
  buf buffer_15 (buffer_15_out, buffer_33_out);
  buf buffer_16 (buffer_16_out, ALU_SET);
  buf buffer_17 (buffer_17_out, buffer_16_out);
  buf buffer_18 (buffer_18_out, buffer_17_out);
  buf buffer_19 (buffer_19_out, buffer_18_out);
  buf buffer_20 (ALU_SET, buffer_13_out);
  Multiplexer #(.width(4)) multiplexer_6 (.in0(4'b0000), .in1(INSTRUCTION[7:4]), .out(REG_SET_SEL), .sel(or_1_out));
  Multiplexer #(.width(16)) multiplexer_7 (.in0({16{1'b0}}), .in1(ALU_IN), .out(REG_SET_VAL), .sel(or_1_out));
  buf buffer_21 (buffer_21_out, or_1_out);
  buf buffer_22 (buffer_22_out, buffer_21_out);
  buf buffer_23 (REG_SET_TRIG, buffer_22_out);
  and and_3 (and_3_out, and_1_out, buffer_305_out);
  buf buffer_24 (buffer_24_out, buffer_26_out);
  buf buffer_25 (buffer_25_out, buffer_24_out);
  buf buffer_26 (buffer_26_out, buffer_27_out);
  buf buffer_27 (buffer_27_out, buffer_28_out);
  buf buffer_28 (buffer_28_out, buffer_45_out);
  buf buffer_29 (buffer_29_out, buffer_14_out);
  buf buffer_30 (buffer_30_out, buffer_29_out);
  buf buffer_31 (buffer_31_out, buffer_30_out);
  buf buffer_32 (buffer_32_out, buffer_31_out);
  buf buffer_33 (buffer_33_out, buffer_34_out);
  buf buffer_34 (buffer_34_out, buffer_35_out);
  buf buffer_35 (buffer_35_out, buffer_36_out);
  buf buffer_36 (buffer_36_out, buffer_53_out);
  buf buffer_37 (buffer_37_out, buffer_19_out);
  buf buffer_38 (buffer_38_out, buffer_37_out);
  buf buffer_39 (buffer_39_out, buffer_38_out);
  buf buffer_40 (buffer_40_out, buffer_39_out);
  buf buffer_41 (buffer_41_out, buffer_25_out);
  buf buffer_42 (buffer_42_out, buffer_41_out);
  buf buffer_43 (buffer_43_out, buffer_42_out);
  buf buffer_44 (buffer_44_out, buffer_43_out);
  buf buffer_45 (buffer_45_out, buffer_46_out);
  buf buffer_46 (buffer_46_out, buffer_47_out);
  buf buffer_47 (buffer_47_out, buffer_48_out);
  buf buffer_48 (buffer_48_out, buffer_65_out);
  buf buffer_49 (buffer_49_out, buffer_32_out);
  buf buffer_50 (buffer_50_out, buffer_49_out);
  buf buffer_51 (buffer_51_out, buffer_50_out);
  buf buffer_52 (buffer_52_out, buffer_51_out);
  buf buffer_53 (buffer_53_out, buffer_54_out);
  buf buffer_54 (buffer_54_out, buffer_55_out);
  buf buffer_55 (buffer_55_out, buffer_56_out);
  buf buffer_56 (buffer_56_out, buffer_73_out);
  buf buffer_57 (buffer_57_out, buffer_40_out);
  buf buffer_58 (buffer_58_out, buffer_57_out);
  buf buffer_59 (buffer_59_out, buffer_58_out);
  buf buffer_60 (buffer_60_out, buffer_59_out);
  buf buffer_61 (buffer_61_out, buffer_44_out);
  buf buffer_62 (buffer_62_out, buffer_61_out);
  buf buffer_63 (buffer_63_out, buffer_62_out);
  buf buffer_64 (buffer_64_out, buffer_63_out);
  buf buffer_65 (buffer_65_out, buffer_66_out);
  buf buffer_66 (buffer_66_out, buffer_67_out);
  buf buffer_67 (buffer_67_out, buffer_68_out);
  buf buffer_68 (buffer_68_out, buffer_92_out);
  buf buffer_69 (buffer_69_out, buffer_52_out);
  buf buffer_70 (buffer_70_out, buffer_69_out);
  buf buffer_71 (buffer_71_out, buffer_70_out);
  buf buffer_72 (buffer_72_out, buffer_71_out);
  buf buffer_73 (buffer_73_out, buffer_74_out);
  buf buffer_74 (buffer_74_out, buffer_75_out);
  buf buffer_75 (buffer_75_out, buffer_76_out);
  buf buffer_76 (buffer_76_out, buffer_100_out);
  buf buffer_77 (buffer_77_out, buffer_60_out);
  buf buffer_78 (buffer_78_out, buffer_77_out);
  buf buffer_79 (buffer_79_out, buffer_78_out);
  buf buffer_80 (buffer_80_out, buffer_79_out);
  buf buffer_81 (buffer_81_out, buffer_84_out);
  buf buffer_82 (buffer_82_out, buffer_81_out);
  buf buffer_83 (buffer_83_out, buffer_82_out);
  buf buffer_84 (buffer_84_out, buffer_85_out);
  buf buffer_85 (buffer_85_out, buffer_86_out);
  buf buffer_86 (buffer_86_out, buffer_87_out);
  buf buffer_87 (buffer_87_out, buffer_112_out);
  buf buffer_88 (buffer_88_out, buffer_64_out);
  buf buffer_89 (buffer_89_out, buffer_88_out);
  buf buffer_90 (buffer_90_out, buffer_89_out);
  buf buffer_91 (buffer_91_out, buffer_90_out);
  buf buffer_92 (buffer_92_out, buffer_93_out);
  buf buffer_93 (buffer_93_out, buffer_94_out);
  buf buffer_94 (buffer_94_out, buffer_95_out);
  buf buffer_95 (buffer_95_out, buffer_120_out);
  buf buffer_96 (buffer_96_out, buffer_72_out);
  buf buffer_97 (buffer_97_out, buffer_96_out);
  buf buffer_98 (buffer_98_out, buffer_97_out);
  buf buffer_99 (buffer_99_out, buffer_98_out);
  buf buffer_100 (buffer_100_out, buffer_101_out);
  buf buffer_101 (buffer_101_out, buffer_102_out);
  buf buffer_102 (buffer_102_out, buffer_103_out);
  buf buffer_103 (buffer_103_out, buffer_127_out);
  buf buffer_104 (buffer_104_out, buffer_80_out);
  buf buffer_105 (buffer_105_out, buffer_104_out);
  buf buffer_106 (buffer_106_out, buffer_105_out);
  buf buffer_107 (buffer_107_out, buffer_106_out);
  buf buffer_108 (buffer_108_out, buffer_83_out);
  buf buffer_109 (buffer_109_out, buffer_108_out);
  buf buffer_110 (buffer_110_out, buffer_109_out);
  buf buffer_111 (buffer_111_out, buffer_110_out);
  buf buffer_112 (buffer_112_out, buffer_113_out);
  buf buffer_113 (buffer_113_out, buffer_114_out);
  buf buffer_114 (buffer_114_out, buffer_115_out);
  buf buffer_115 (buffer_115_out, buffer_139_out);
  buf buffer_116 (buffer_116_out, buffer_91_out);
  buf buffer_117 (buffer_117_out, buffer_116_out);
  buf buffer_118 (buffer_118_out, buffer_117_out);
  buf buffer_119 (buffer_119_out, buffer_118_out);
  buf buffer_120 (buffer_120_out, buffer_121_out);
  buf buffer_121 (buffer_121_out, buffer_122_out);
  buf buffer_122 (buffer_122_out, buffer_147_out);
  buf buffer_123 (buffer_123_out, buffer_99_out);
  buf buffer_124 (buffer_124_out, buffer_123_out);
  buf buffer_125 (buffer_125_out, buffer_124_out);
  buf buffer_126 (buffer_126_out, buffer_125_out);
  buf buffer_127 (buffer_127_out, buffer_128_out);
  buf buffer_128 (buffer_128_out, buffer_129_out);
  buf buffer_129 (buffer_129_out, buffer_130_out);
  buf buffer_130 (buffer_130_out, buffer_155_out);
  buf buffer_131 (buffer_131_out, buffer_107_out);
  buf buffer_132 (buffer_132_out, buffer_131_out);
  buf buffer_133 (buffer_133_out, buffer_132_out);
  buf buffer_134 (buffer_134_out, buffer_133_out);
  buf buffer_135 (buffer_135_out, buffer_111_out);
  buf buffer_136 (buffer_136_out, buffer_135_out);
  buf buffer_137 (buffer_137_out, buffer_136_out);
  buf buffer_138 (buffer_138_out, buffer_137_out);
  buf buffer_139 (buffer_139_out, buffer_140_out);
  buf buffer_140 (buffer_140_out, buffer_141_out);
  buf buffer_141 (buffer_141_out, buffer_142_out);
  buf buffer_142 (buffer_142_out, buffer_168_out);
  buf buffer_143 (buffer_143_out, buffer_119_out);
  buf buffer_144 (buffer_144_out, buffer_143_out);
  buf buffer_145 (buffer_145_out, buffer_144_out);
  buf buffer_146 (buffer_146_out, buffer_145_out);
  buf buffer_147 (buffer_147_out, buffer_148_out);
  buf buffer_148 (buffer_148_out, buffer_149_out);
  buf buffer_149 (buffer_149_out, buffer_150_out);
  buf buffer_150 (buffer_150_out, buffer_176_out);
  buf buffer_151 (buffer_151_out, buffer_126_out);
  buf buffer_152 (buffer_152_out, buffer_151_out);
  buf buffer_153 (buffer_153_out, buffer_152_out);
  buf buffer_154 (buffer_154_out, buffer_153_out);
  buf buffer_155 (buffer_155_out, buffer_156_out);
  buf buffer_156 (buffer_156_out, buffer_157_out);
  buf buffer_157 (buffer_157_out, buffer_161_out);
  buf buffer_158 (buffer_158_out, buffer_134_out);
  buf buffer_159 (buffer_159_out, buffer_158_out);
  buf buffer_160 (buffer_160_out, buffer_159_out);
  buf buffer_161 (buffer_161_out, buffer_160_out);
  buf buffer_162 (buffer_162_out, buffer_165_out);
  buf buffer_163 (buffer_163_out, buffer_162_out);
  buf buffer_164 (buffer_164_out, buffer_138_out);
  buf buffer_165 (buffer_165_out, buffer_164_out);
  buf buffer_166 (buffer_166_out, buffer_167_out);
  buf buffer_167 (buffer_167_out, buffer_186_out);
  buf buffer_168 (buffer_168_out, buffer_169_out);
  buf buffer_169 (buffer_169_out, buffer_166_out);
  buf buffer_170 (buffer_170_out, buffer_173_out);
  buf buffer_171 (buffer_171_out, buffer_170_out);
  buf buffer_172 (buffer_172_out, buffer_146_out);
  buf buffer_173 (buffer_173_out, buffer_172_out);
  buf buffer_174 (buffer_174_out, buffer_175_out);
  buf buffer_175 (buffer_175_out, buffer_194_out);
  buf buffer_176 (buffer_176_out, buffer_177_out);
  buf buffer_177 (buffer_177_out, buffer_174_out);
  buf buffer_178 (buffer_178_out, buffer_181_out);
  buf buffer_179 (buffer_179_out, buffer_178_out);
  buf buffer_180 (buffer_180_out, buffer_154_out);
  buf buffer_181 (buffer_181_out, buffer_180_out);
  buf buffer_182 (buffer_182_out, buffer_163_out);
  buf buffer_183 (buffer_183_out, buffer_182_out);
  buf buffer_184 (buffer_184_out, buffer_183_out);
  buf buffer_185 (buffer_185_out, buffer_184_out);
  buf buffer_186 (buffer_186_out, buffer_187_out);
  buf buffer_187 (buffer_187_out, buffer_188_out);
  buf buffer_188 (buffer_188_out, buffer_189_out);
  buf buffer_189 (buffer_189_out, buffer_206_out);
  buf buffer_190 (buffer_190_out, buffer_171_out);
  buf buffer_191 (buffer_191_out, buffer_190_out);
  buf buffer_192 (buffer_192_out, buffer_191_out);
  buf buffer_193 (buffer_193_out, buffer_192_out);
  buf buffer_194 (buffer_194_out, buffer_195_out);
  buf buffer_195 (buffer_195_out, buffer_196_out);
  buf buffer_196 (buffer_196_out, buffer_197_out);
  buf buffer_197 (buffer_197_out, buffer_214_out);
  buf buffer_198 (buffer_198_out, buffer_179_out);
  buf buffer_199 (buffer_199_out, buffer_198_out);
  buf buffer_200 (buffer_200_out, buffer_199_out);
  buf buffer_201 (buffer_201_out, buffer_200_out);
  buf buffer_202 (buffer_202_out, buffer_185_out);
  buf buffer_203 (buffer_203_out, buffer_202_out);
  buf buffer_204 (buffer_204_out, buffer_203_out);
  buf buffer_205 (buffer_205_out, buffer_204_out);
  buf buffer_206 (buffer_206_out, buffer_207_out);
  buf buffer_207 (buffer_207_out, buffer_208_out);
  buf buffer_208 (buffer_208_out, buffer_209_out);
  buf buffer_209 (buffer_209_out, buffer_226_out);
  buf buffer_210 (buffer_210_out, buffer_193_out);
  buf buffer_211 (buffer_211_out, buffer_210_out);
  buf buffer_212 (buffer_212_out, buffer_211_out);
  buf buffer_213 (buffer_213_out, buffer_212_out);
  buf buffer_214 (buffer_214_out, buffer_215_out);
  buf buffer_215 (buffer_215_out, buffer_216_out);
  buf buffer_216 (buffer_216_out, buffer_217_out);
  buf buffer_217 (buffer_217_out, buffer_234_out);
  buf buffer_218 (buffer_218_out, buffer_201_out);
  buf buffer_219 (buffer_219_out, buffer_218_out);
  buf buffer_220 (buffer_220_out, buffer_219_out);
  buf buffer_221 (buffer_221_out, buffer_220_out);
  buf buffer_222 (buffer_222_out, buffer_205_out);
  buf buffer_223 (buffer_223_out, buffer_222_out);
  buf buffer_224 (buffer_224_out, buffer_223_out);
  buf buffer_225 (buffer_225_out, buffer_224_out);
  buf buffer_226 (buffer_226_out, buffer_227_out);
  buf buffer_227 (buffer_227_out, buffer_228_out);
  buf buffer_228 (buffer_228_out, buffer_229_out);
  buf buffer_229 (buffer_229_out, buffer_246_out);
  buf buffer_230 (buffer_230_out, buffer_213_out);
  buf buffer_231 (buffer_231_out, buffer_230_out);
  buf buffer_232 (buffer_232_out, buffer_231_out);
  buf buffer_233 (buffer_233_out, buffer_232_out);
  buf buffer_234 (buffer_234_out, buffer_235_out);
  buf buffer_235 (buffer_235_out, buffer_236_out);
  buf buffer_236 (buffer_236_out, buffer_237_out);
  buf buffer_237 (buffer_237_out, buffer_254_out);
  buf buffer_238 (buffer_238_out, buffer_221_out);
  buf buffer_239 (buffer_239_out, buffer_238_out);
  buf buffer_240 (buffer_240_out, buffer_239_out);
  buf buffer_241 (buffer_241_out, buffer_240_out);
  buf buffer_242 (buffer_242_out, buffer_225_out);
  buf buffer_243 (buffer_243_out, buffer_242_out);
  buf buffer_244 (buffer_244_out, buffer_243_out);
  buf buffer_245 (buffer_245_out, buffer_244_out);
  buf buffer_246 (buffer_246_out, buffer_247_out);
  buf buffer_247 (buffer_247_out, buffer_248_out);
  buf buffer_248 (buffer_248_out, buffer_249_out);
  buf buffer_249 (buffer_249_out, buffer_266_out);
  buf buffer_250 (buffer_250_out, buffer_233_out);
  buf buffer_251 (buffer_251_out, buffer_250_out);
  buf buffer_252 (buffer_252_out, buffer_251_out);
  buf buffer_253 (buffer_253_out, buffer_252_out);
  buf buffer_254 (buffer_254_out, buffer_255_out);
  buf buffer_255 (buffer_255_out, buffer_256_out);
  buf buffer_256 (buffer_256_out, buffer_257_out);
  buf buffer_257 (buffer_257_out, buffer_274_out);
  buf buffer_258 (buffer_258_out, buffer_241_out);
  buf buffer_259 (buffer_259_out, buffer_258_out);
  buf buffer_260 (buffer_260_out, buffer_259_out);
  buf buffer_261 (buffer_261_out, buffer_260_out);
  buf buffer_262 (buffer_262_out, buffer_245_out);
  buf buffer_263 (buffer_263_out, buffer_262_out);
  buf buffer_264 (buffer_264_out, buffer_263_out);
  buf buffer_265 (buffer_265_out, buffer_264_out);
  buf buffer_266 (buffer_266_out, buffer_267_out);
  buf buffer_267 (buffer_267_out, buffer_268_out);
  buf buffer_268 (buffer_268_out, buffer_269_out);
  buf buffer_269 (buffer_269_out, buffer_286_out);
  buf buffer_270 (buffer_270_out, buffer_253_out);
  buf buffer_271 (buffer_271_out, buffer_270_out);
  buf buffer_272 (buffer_272_out, buffer_271_out);
  buf buffer_273 (buffer_273_out, buffer_272_out);
  buf buffer_274 (buffer_274_out, buffer_275_out);
  buf buffer_275 (buffer_275_out, buffer_276_out);
  buf buffer_276 (buffer_276_out, buffer_277_out);
  buf buffer_277 (buffer_277_out, buffer_294_out);
  buf buffer_278 (buffer_278_out, buffer_261_out);
  buf buffer_279 (buffer_279_out, buffer_278_out);
  buf buffer_280 (buffer_280_out, buffer_279_out);
  buf buffer_281 (buffer_281_out, buffer_280_out);
  buf buffer_282 (buffer_282_out, buffer_265_out);
  buf buffer_283 (buffer_283_out, buffer_282_out);
  buf buffer_284 (buffer_284_out, buffer_283_out);
  buf buffer_285 (buffer_285_out, buffer_284_out);
  buf buffer_286 (buffer_286_out, buffer_287_out);
  buf buffer_287 (buffer_287_out, buffer_288_out);
  buf buffer_288 (buffer_288_out, buffer_289_out);
  buf buffer_289 (buffer_289_out, buffer_306_out);
  buf buffer_290 (buffer_290_out, buffer_273_out);
  buf buffer_291 (buffer_291_out, buffer_290_out);
  buf buffer_292 (buffer_292_out, buffer_291_out);
  buf buffer_293 (buffer_293_out, buffer_292_out);
  buf buffer_294 (buffer_294_out, buffer_295_out);
  buf buffer_295 (buffer_295_out, buffer_296_out);
  buf buffer_296 (buffer_296_out, buffer_297_out);
  buf buffer_297 (buffer_297_out, buffer_311_out);
  buf buffer_298 (buffer_298_out, buffer_281_out);
  buf buffer_299 (buffer_299_out, buffer_298_out);
  buf buffer_300 (buffer_300_out, buffer_299_out);
  buf buffer_301 (buffer_301_out, buffer_300_out);
  buf buffer_302 (buffer_302_out, buffer_285_out);
  buf buffer_303 (buffer_303_out, buffer_302_out);
  buf buffer_304 (buffer_304_out, buffer_303_out);
  buf buffer_305 (buffer_305_out, buffer_304_out);
  buf buffer_306 (buffer_306_out, buffer_333_out);
  buf buffer_307 (buffer_307_out, buffer_293_out);
  buf buffer_308 (buffer_308_out, buffer_307_out);
  buf buffer_309 (buffer_309_out, buffer_308_out);
  buf buffer_310 (buffer_310_out, buffer_309_out);
  buf buffer_311 (buffer_311_out, buffer_312_out);
  buf buffer_312 (buffer_312_out, buffer_313_out);
  buf buffer_313 (buffer_313_out, buffer_314_out);
  buf buffer_314 (buffer_314_out, buffer_323_out);
  buf buffer_315 (buffer_315_out, buffer_301_out);
  buf buffer_316 (buffer_316_out, buffer_315_out);
  buf buffer_317 (buffer_317_out, buffer_316_out);
  buf buffer_318 (buffer_318_out, buffer_317_out);
  buf buffer_319 (buffer_319_out, buffer_310_out);
  buf buffer_320 (buffer_320_out, buffer_319_out);
  buf buffer_321 (buffer_321_out, buffer_320_out);
  buf buffer_322 (buffer_322_out, buffer_321_out);
  buf buffer_323 (buffer_323_out, buffer_324_out);
  buf buffer_324 (buffer_324_out, buffer_325_out);
  buf buffer_325 (buffer_325_out, buffer_326_out);
  buf buffer_326 (buffer_326_out, buffer_334_out);
  buf buffer_327 (buffer_327_out, buffer_318_out);
  buf buffer_328 (buffer_328_out, buffer_327_out);
  buf buffer_329 (buffer_329_out, buffer_328_out);
  buf buffer_330 (buffer_330_out, buffer_329_out);
  buf buffer_331 (buffer_331_out, buffer_322_out);
  buf buffer_332 (buffer_332_out, buffer_331_out);
  buf buffer_333 (buffer_333_out, buffer_332_out);
  buf buffer_334 (buffer_334_out, buffer_340_out);
  buf buffer_335 (buffer_335_out, buffer_330_out);
  buf buffer_336 (buffer_336_out, buffer_335_out);
  buf buffer_337 (buffer_337_out, buffer_336_out);
  buf buffer_338 (buffer_338_out, buffer_337_out);
  buf buffer_339 (buffer_339_out, buffer_338_out);
  buf buffer_340 (buffer_340_out, buffer_339_out);

  // Notes on the sheet:
  //   Multiplication takes forever :(
endmodule

module ALU_SECTION_2 (
  input  [11:0] INSTRUCTION,
  input  CLK,
  input  [15:0] NEXT_BYTE,
  input  [15:0] REG_IN,
  input  [15:0] ALU_IN,
  output [3:0] REG_SEL_OUT,
  output [15:0] ALU_OUT_0,
  output [15:0] ALU_OUT_1,
  output [2:0] ALU_OP,
  output ALU_SET,
  output [3:0] REG_OUT_SEL,
  output [15:0] REG_OUT_VAL,
  output REG_SET_TRIG
);

  wire and_1_out, and_2_out, and_3_out, buffer_1_out, buffer_2_out, buffer_3_out, buffer_4_out, buffer_5_out,
       buffer_6_out, buffer_7_out, buffer_8_out, buffer_9_out, buffer_10_out, buffer_11_out, buffer_12_out,
       buffer_13_out, buffer_14_out, buffer_15_out, buffer_16_out, buffer_17_out, buffer_18_out,
       buffer_19_out, buffer_20_out, buffer_21_out, buffer_22_out, buffer_23_out, buffer_24_out,
       buffer_25_out, buffer_26_out, buffer_28_out, buffer_29_out, buffer_30_out, buffer_31_out,
       buffer_32_out, buffer_33_out, buffer_34_out, buffer_35_out, buffer_36_out, buffer_37_out,
       buffer_38_out, buffer_39_out, buffer_40_out, buffer_41_out, buffer_42_out, buffer_43_out,
       buffer_44_out, buffer_45_out, buffer_46_out, buffer_47_out, buffer_48_out, buffer_49_out,
       buffer_50_out, buffer_52_out, buffer_53_out, buffer_54_out, buffer_55_out, buffer_56_out,
       buffer_57_out, buffer_58_out, buffer_59_out, buffer_60_out, buffer_61_out, buffer_62_out,
       buffer_63_out, buffer_64_out, buffer_65_out, buffer_66_out, buffer_67_out, buffer_68_out,
       buffer_69_out, buffer_70_out, buffer_71_out, buffer_72_out, buffer_73_out, buffer_74_out,
       buffer_75_out, buffer_76_out, buffer_77_out, buffer_78_out, buffer_79_out, buffer_80_out,
       buffer_81_out, buffer_82_out, buffer_83_out, buffer_84_out, buffer_85_out, buffer_86_out,
       buffer_87_out, buffer_88_out, buffer_89_out, buffer_90_out, buffer_91_out, buffer_92_out,
       buffer_93_out, buffer_94_out, buffer_95_out, buffer_96_out, buffer_97_out, buffer_98_out,
       buffer_99_out, buffer_100_out, buffer_101_out, buffer_102_out, buffer_103_out, buffer_104_out,
       buffer_105_out, buffer_106_out, buffer_107_out, buffer_108_out, buffer_109_out, buffer_110_out,
       buffer_111_out, buffer_112_out, buffer_113_out, buffer_114_out, buffer_115_out, buffer_116_out,
       buffer_117_out, buffer_118_out, buffer_119_out, buffer_120_out, buffer_121_out, buffer_122_out,
       buffer_123_out, buffer_124_out, buffer_125_out, buffer_126_out, buffer_127_out, buffer_128_out,
       buffer_129_out, buffer_130_out, buffer_131_out, buffer_132_out, buffer_133_out, buffer_134_out,
       buffer_135_out, buffer_136_out, buffer_137_out, buffer_138_out, buffer_139_out, buffer_140_out,
       buffer_141_out, buffer_142_out, buffer_143_out, buffer_144_out, buffer_145_out, buffer_146_out,
       buffer_147_out, buffer_148_out, buffer_149_out, buffer_150_out, buffer_151_out, buffer_152_out,
       buffer_153_out, buffer_154_out, buffer_155_out, buffer_156_out, buffer_157_out, buffer_158_out,
       buffer_159_out, buffer_160_out, buffer_161_out, buffer_162_out, buffer_163_out, buffer_164_out,
       buffer_165_out, buffer_166_out, buffer_167_out, buffer_168_out, buffer_169_out, buffer_170_out,
       buffer_171_out, buffer_172_out, buffer_173_out, buffer_174_out, buffer_175_out, buffer_176_out,
       buffer_177_out, buffer_178_out, buffer_179_out, buffer_180_out, buffer_181_out, buffer_182_out,
       buffer_183_out, buffer_184_out, buffer_185_out, buffer_186_out, buffer_187_out, buffer_188_out,
       buffer_189_out, buffer_190_out, buffer_191_out, buffer_192_out, buffer_193_out, buffer_194_out,
       buffer_195_out, buffer_196_out, buffer_197_out, buffer_198_out, buffer_199_out, buffer_200_out,
       buffer_201_out, buffer_202_out, buffer_203_out, buffer_204_out, buffer_205_out, buffer_206_out,
       buffer_207_out, buffer_208_out, buffer_209_out, buffer_210_out, buffer_211_out, buffer_212_out,
       buffer_213_out, buffer_214_out, buffer_215_out, buffer_216_out, buffer_217_out, buffer_218_out,
       buffer_219_out, buffer_220_out, buffer_221_out, buffer_222_out, buffer_223_out, buffer_224_out,
       buffer_225_out, buffer_226_out, buffer_227_out, buffer_228_out, buffer_229_out, buffer_230_out,
       buffer_231_out, buffer_232_out, buffer_233_out, buffer_234_out, buffer_235_out, buffer_236_out,
       buffer_237_out, buffer_238_out, buffer_239_out, buffer_240_out, buffer_241_out, buffer_242_out,
       buffer_243_out, buffer_244_out, buffer_245_out, buffer_246_out, buffer_247_out, buffer_248_out,
       buffer_249_out, buffer_250_out, buffer_251_out, buffer_252_out, buffer_253_out, buffer_254_out,
       buffer_255_out, buffer_256_out, buffer_257_out, buffer_258_out, buffer_259_out, buffer_260_out,
       buffer_261_out, buffer_262_out, buffer_263_out, buffer_264_out, buffer_265_out, buffer_266_out,
       buffer_267_out, buffer_268_out, buffer_269_out, buffer_270_out, buffer_271_out, buffer_272_out,
       buffer_273_out, buffer_274_out, buffer_275_out, buffer_276_out, buffer_277_out, buffer_278_out,
       buffer_279_out, buffer_280_out, buffer_281_out, buffer_282_out, buffer_283_out, buffer_284_out,
       buffer_285_out, buffer_286_out, buffer_287_out, buffer_288_out, buffer_289_out, buffer_290_out,
       buffer_291_out, buffer_292_out, buffer_293_out, buffer_294_out, buffer_295_out, buffer_296_out,
       buffer_297_out, buffer_298_out, buffer_299_out, buffer_300_out, buffer_301_out, buffer_302_out,
       buffer_303_out, buffer_304_out, buffer_305_out, buffer_306_out, buffer_307_out, buffer_308_out,
       buffer_309_out, buffer_310_out, buffer_311_out, buffer_312_out, buffer_313_out, buffer_314_out,
       buffer_315_out, buffer_316_out, buffer_317_out, buffer_318_out, buffer_319_out, buffer_320_out,
       buffer_321_out, buffer_322_out, buffer_323_out, buffer_324_out, buffer_325_out, buffer_326_out,
       buffer_327_out, buffer_328_out, buffer_329_out, buffer_330_out, buffer_331_out, buffer_332_out,
       buffer_333_out, buffer_334_out, buffer_335_out, buffer_336_out, buffer_337_out, buffer_338_out,
       buffer_339_out, buffer_340_out, buffer_341_out, not_1_out, not_2_out, or_1_out;
  wire [2:0] xnor_1_out;
  wire [15:0] multiplexer_2_out, multiplexer_3_out;

  Multiplexer #(.width(4)) multiplexer_1 (.in0(4'b0000), .in1(INSTRUCTION[3:0]), .out(REG_SEL_OUT), .sel(CLK));
  buf buffer_1 (buffer_1_out, CLK);
  buf buffer_2 (buffer_2_out, buffer_1_out);
  buf buffer_3 (buffer_3_out, buffer_2_out);
  buf buffer_4 (buffer_4_out, buffer_3_out);
  buf buffer_5 (buffer_5_out, buffer_4_out);
  buf buffer_6 (buffer_6_out, buffer_5_out);
  Multiplexer #(.width(16)) multiplexer_2 (
    .in0(REG_IN), .in1(NEXT_BYTE), .out(multiplexer_2_out), .sel(INSTRUCTION[11]));
  Multiplexer #(.width(16)) multiplexer_3 (
    .in0(NEXT_BYTE), .in1(REG_IN), .out(multiplexer_3_out), .sel(INSTRUCTION[11]));
  assign xnor_1_out = ~(INSTRUCTION[10:8] ^ 3'b010);  // XNOR_Gate xnor_1, 3 bits wide
  and and_1 (and_1_out, xnor_1_out[0], xnor_1_out[1], xnor_1_out[2]);
  buf buffer_7 (buffer_7_out, buffer_49_out);
  buf buffer_8 (buffer_8_out, buffer_7_out);
  buf buffer_9 (buffer_9_out, buffer_6_out);
  buf buffer_10 (buffer_10_out, buffer_9_out);
  buf buffer_11 (buffer_11_out, buffer_10_out);
  buf buffer_12 (buffer_12_out, buffer_11_out);
  Multiplexer #(.width(16)) multiplexer_4 (
    .in0({16{1'b0}}), .in1(multiplexer_2_out), .out(ALU_OUT_0), .sel(buffer_49_out));
  Multiplexer #(.width(16)) multiplexer_5 (
    .in0({16{1'b0}}), .in1(multiplexer_3_out), .out(ALU_OUT_1), .sel(buffer_49_out));
  Multiplexer #(.width(3)) multiplexer_6 (.in0(3'b000), .in1(INSTRUCTION[10:8]), .out(ALU_OP), .sel(buffer_49_out));
  buf buffer_13 (buffer_13_out, buffer_49_out);
  buf buffer_14 (buffer_14_out, buffer_13_out);
  or or_1 (or_1_out, and_2_out, and_3_out);
  and and_2 (and_2_out, ~and_1_out, buffer_19_out);  // AND_Gate
  and and_3 (and_3_out, and_1_out, buffer_313_out);
  buf buffer_15 (buffer_15_out, buffer_33_out);
  buf buffer_16 (buffer_16_out, buffer_19_out);
  buf buffer_17 (buffer_17_out, buffer_16_out);
  buf buffer_18 (buffer_18_out, buffer_17_out);
  buf buffer_19 (buffer_19_out, buffer_20_out);
  buf buffer_20 (buffer_20_out, buffer_21_out);
  buf buffer_21 (buffer_21_out, buffer_41_out);
  buf buffer_22 (buffer_22_out, buffer_8_out);
  buf buffer_23 (buffer_23_out, buffer_22_out);
  buf buffer_24 (buffer_24_out, buffer_23_out);
  buf buffer_25 (buffer_25_out, buffer_24_out);
  buf buffer_26 (buffer_26_out, buffer_12_out);
  not not_1 (not_1_out, buffer_26_out);
  buf buffer_27 (ALU_SET, buffer_14_out);
  Multiplexer #(.width(4)) multiplexer_7 (.in0(4'b0000), .in1(INSTRUCTION[7:4]), .out(REG_OUT_SEL), .sel(or_1_out));
  Multiplexer #(.width(16)) multiplexer_8 (.in0({16{1'b0}}), .in1(ALU_IN), .out(REG_OUT_VAL), .sel(or_1_out));
  buf buffer_28 (buffer_28_out, or_1_out);
  buf buffer_29 (buffer_29_out, buffer_15_out);
  buf buffer_30 (buffer_30_out, buffer_29_out);
  buf buffer_31 (buffer_31_out, buffer_30_out);
  buf buffer_32 (buffer_32_out, buffer_31_out);
  buf buffer_33 (buffer_33_out, buffer_34_out);
  buf buffer_34 (buffer_34_out, buffer_35_out);
  buf buffer_35 (buffer_35_out, buffer_36_out);
  buf buffer_36 (buffer_36_out, buffer_56_out);
  buf buffer_37 (buffer_37_out, buffer_18_out);
  buf buffer_38 (buffer_38_out, buffer_37_out);
  buf buffer_39 (buffer_39_out, buffer_38_out);
  buf buffer_40 (buffer_40_out, buffer_39_out);
  buf buffer_41 (buffer_41_out, buffer_42_out);
  buf buffer_42 (buffer_42_out, buffer_43_out);
  buf buffer_43 (buffer_43_out, buffer_44_out);
  buf buffer_44 (buffer_44_out, buffer_64_out);
  buf buffer_45 (buffer_45_out, buffer_25_out);
  buf buffer_46 (buffer_46_out, buffer_45_out);
  buf buffer_47 (buffer_47_out, buffer_46_out);
  buf buffer_48 (buffer_48_out, buffer_47_out);
  not not_2 (not_2_out, not_1_out);
  buf buffer_49 (buffer_49_out, not_2_out);
  buf buffer_50 (buffer_50_out, buffer_28_out);
  buf buffer_51 (REG_SET_TRIG, buffer_50_out);
  buf buffer_52 (buffer_52_out, buffer_32_out);
  buf buffer_53 (buffer_53_out, buffer_52_out);
  buf buffer_54 (buffer_54_out, buffer_53_out);
  buf buffer_55 (buffer_55_out, buffer_54_out);
  buf buffer_56 (buffer_56_out, buffer_57_out);
  buf buffer_57 (buffer_57_out, buffer_58_out);
  buf buffer_58 (buffer_58_out, buffer_59_out);
  buf buffer_59 (buffer_59_out, buffer_79_out);
  buf buffer_60 (buffer_60_out, buffer_40_out);
  buf buffer_61 (buffer_61_out, buffer_60_out);
  buf buffer_62 (buffer_62_out, buffer_61_out);
  buf buffer_63 (buffer_63_out, buffer_62_out);
  buf buffer_64 (buffer_64_out, buffer_65_out);
  buf buffer_65 (buffer_65_out, buffer_66_out);
  buf buffer_66 (buffer_66_out, buffer_67_out);
  buf buffer_67 (buffer_67_out, buffer_87_out);
  buf buffer_68 (buffer_68_out, buffer_48_out);
  buf buffer_69 (buffer_69_out, buffer_68_out);
  buf buffer_70 (buffer_70_out, buffer_69_out);
  buf buffer_71 (buffer_71_out, buffer_70_out);
  buf buffer_72 (buffer_72_out, buffer_73_out);
  buf buffer_73 (buffer_73_out, buffer_74_out);
  buf buffer_74 (buffer_74_out, buffer_99_out);
  buf buffer_75 (buffer_75_out, buffer_55_out);
  buf buffer_76 (buffer_76_out, buffer_75_out);
  buf buffer_77 (buffer_77_out, buffer_76_out);
  buf buffer_78 (buffer_78_out, buffer_77_out);
  buf buffer_79 (buffer_79_out, buffer_80_out);
  buf buffer_80 (buffer_80_out, buffer_81_out);
  buf buffer_81 (buffer_81_out, buffer_82_out);
  buf buffer_82 (buffer_82_out, buffer_107_out);
  buf buffer_83 (buffer_83_out, buffer_63_out);
  buf buffer_84 (buffer_84_out, buffer_83_out);
  buf buffer_85 (buffer_85_out, buffer_84_out);
  buf buffer_86 (buffer_86_out, buffer_85_out);
  buf buffer_87 (buffer_87_out, buffer_88_out);
  buf buffer_88 (buffer_88_out, buffer_89_out);
  buf buffer_89 (buffer_89_out, buffer_90_out);
  buf buffer_90 (buffer_90_out, buffer_115_out);
  buf buffer_91 (buffer_91_out, buffer_71_out);
  buf buffer_92 (buffer_92_out, buffer_91_out);
  buf buffer_93 (buffer_93_out, buffer_92_out);
  buf buffer_94 (buffer_94_out, buffer_93_out);
  buf buffer_95 (buffer_95_out, buffer_72_out);
  buf buffer_96 (buffer_96_out, buffer_95_out);
  buf buffer_97 (buffer_97_out, buffer_96_out);
  buf buffer_98 (buffer_98_out, buffer_97_out);
  buf buffer_99 (buffer_99_out, buffer_100_out);
  buf buffer_100 (buffer_100_out, buffer_101_out);
  buf buffer_101 (buffer_101_out, buffer_102_out);
  buf buffer_102 (buffer_102_out, buffer_127_out);
  buf buffer_103 (buffer_103_out, buffer_78_out);
  buf buffer_104 (buffer_104_out, buffer_103_out);
  buf buffer_105 (buffer_105_out, buffer_104_out);
  buf buffer_106 (buffer_106_out, buffer_105_out);
  buf buffer_107 (buffer_107_out, buffer_108_out);
  buf buffer_108 (buffer_108_out, buffer_109_out);
  buf buffer_109 (buffer_109_out, buffer_110_out);
  buf buffer_110 (buffer_110_out, buffer_135_out);
  buf buffer_111 (buffer_111_out, buffer_86_out);
  buf buffer_112 (buffer_112_out, buffer_111_out);
  buf buffer_113 (buffer_113_out, buffer_112_out);
  buf buffer_114 (buffer_114_out, buffer_113_out);
  buf buffer_115 (buffer_115_out, buffer_116_out);
  buf buffer_116 (buffer_116_out, buffer_117_out);
  buf buffer_117 (buffer_117_out, buffer_118_out);
  buf buffer_118 (buffer_118_out, buffer_142_out);
  buf buffer_119 (buffer_119_out, buffer_94_out);
  buf buffer_120 (buffer_120_out, buffer_119_out);
  buf buffer_121 (buffer_121_out, buffer_120_out);
  buf buffer_122 (buffer_122_out, buffer_121_out);
  buf buffer_123 (buffer_123_out, buffer_98_out);
  buf buffer_124 (buffer_124_out, buffer_123_out);
  buf buffer_125 (buffer_125_out, buffer_124_out);
  buf buffer_126 (buffer_126_out, buffer_125_out);
  buf buffer_127 (buffer_127_out, buffer_128_out);
  buf buffer_128 (buffer_128_out, buffer_129_out);
  buf buffer_129 (buffer_129_out, buffer_130_out);
  buf buffer_130 (buffer_130_out, buffer_156_out);
  buf buffer_131 (buffer_131_out, buffer_106_out);
  buf buffer_132 (buffer_132_out, buffer_131_out);
  buf buffer_133 (buffer_133_out, buffer_132_out);
  buf buffer_134 (buffer_134_out, buffer_133_out);
  buf buffer_135 (buffer_135_out, buffer_136_out);
  buf buffer_136 (buffer_136_out, buffer_137_out);
  buf buffer_137 (buffer_137_out, buffer_164_out);
  buf buffer_138 (buffer_138_out, buffer_114_out);
  buf buffer_139 (buffer_139_out, buffer_138_out);
  buf buffer_140 (buffer_140_out, buffer_139_out);
  buf buffer_141 (buffer_141_out, buffer_140_out);
  buf buffer_142 (buffer_142_out, buffer_143_out);
  buf buffer_143 (buffer_143_out, buffer_144_out);
  buf buffer_144 (buffer_144_out, buffer_145_out);
  buf buffer_145 (buffer_145_out, buffer_170_out);
  buf buffer_146 (buffer_146_out, buffer_122_out);
  buf buffer_147 (buffer_147_out, buffer_146_out);
  buf buffer_148 (buffer_148_out, buffer_147_out);
  buf buffer_149 (buffer_149_out, buffer_148_out);
  buf buffer_150 (buffer_150_out, buffer_153_out);
  buf buffer_151 (buffer_151_out, buffer_150_out);
  buf buffer_152 (buffer_152_out, buffer_126_out);
  buf buffer_153 (buffer_153_out, buffer_152_out);
  buf buffer_154 (buffer_154_out, buffer_155_out);
  buf buffer_155 (buffer_155_out, buffer_177_out);
  buf buffer_156 (buffer_156_out, buffer_157_out);
  buf buffer_157 (buffer_157_out, buffer_154_out);
  buf buffer_158 (buffer_158_out, buffer_161_out);
  buf buffer_159 (buffer_159_out, buffer_158_out);
  buf buffer_160 (buffer_160_out, buffer_134_out);
  buf buffer_161 (buffer_161_out, buffer_160_out);
  buf buffer_162 (buffer_162_out, buffer_163_out);
  buf buffer_163 (buffer_163_out, buffer_185_out);
  buf buffer_164 (buffer_164_out, buffer_165_out);
  buf buffer_165 (buffer_165_out, buffer_162_out);
  buf buffer_166 (buffer_166_out, buffer_169_out);
  buf buffer_167 (buffer_167_out, buffer_166_out);
  buf buffer_168 (buffer_168_out, buffer_141_out);
  buf buffer_169 (buffer_169_out, buffer_168_out);
  buf buffer_170 (buffer_170_out, buffer_172_out);
  buf buffer_171 (buffer_171_out, buffer_149_out);
  buf buffer_172 (buffer_172_out, buffer_171_out);
  buf buffer_173 (buffer_173_out, buffer_151_out);
  buf buffer_174 (buffer_174_out, buffer_173_out);
  buf buffer_175 (buffer_175_out, buffer_174_out);
  buf buffer_176 (buffer_176_out, buffer_175_out);
  buf buffer_177 (buffer_177_out, buffer_178_out);
  buf buffer_178 (buffer_178_out, buffer_179_out);
  buf buffer_179 (buffer_179_out, buffer_180_out);
  buf buffer_180 (buffer_180_out, buffer_197_out);
  buf buffer_181 (buffer_181_out, buffer_159_out);
  buf buffer_182 (buffer_182_out, buffer_181_out);
  buf buffer_183 (buffer_183_out, buffer_182_out);
  buf buffer_184 (buffer_184_out, buffer_183_out);
  buf buffer_185 (buffer_185_out, buffer_186_out);
  buf buffer_186 (buffer_186_out, buffer_187_out);
  buf buffer_187 (buffer_187_out, buffer_188_out);
  buf buffer_188 (buffer_188_out, buffer_205_out);
  buf buffer_189 (buffer_189_out, buffer_167_out);
  buf buffer_190 (buffer_190_out, buffer_189_out);
  buf buffer_191 (buffer_191_out, buffer_190_out);
  buf buffer_192 (buffer_192_out, buffer_191_out);
  buf buffer_193 (buffer_193_out, buffer_176_out);
  buf buffer_194 (buffer_194_out, buffer_193_out);
  buf buffer_195 (buffer_195_out, buffer_194_out);
  buf buffer_196 (buffer_196_out, buffer_195_out);
  buf buffer_197 (buffer_197_out, buffer_198_out);
  buf buffer_198 (buffer_198_out, buffer_199_out);
  buf buffer_199 (buffer_199_out, buffer_200_out);
  buf buffer_200 (buffer_200_out, buffer_217_out);
  buf buffer_201 (buffer_201_out, buffer_184_out);
  buf buffer_202 (buffer_202_out, buffer_201_out);
  buf buffer_203 (buffer_203_out, buffer_202_out);
  buf buffer_204 (buffer_204_out, buffer_203_out);
  buf buffer_205 (buffer_205_out, buffer_206_out);
  buf buffer_206 (buffer_206_out, buffer_207_out);
  buf buffer_207 (buffer_207_out, buffer_208_out);
  buf buffer_208 (buffer_208_out, buffer_225_out);
  buf buffer_209 (buffer_209_out, buffer_192_out);
  buf buffer_210 (buffer_210_out, buffer_209_out);
  buf buffer_211 (buffer_211_out, buffer_210_out);
  buf buffer_212 (buffer_212_out, buffer_211_out);
  buf buffer_213 (buffer_213_out, buffer_196_out);
  buf buffer_214 (buffer_214_out, buffer_213_out);
  buf buffer_215 (buffer_215_out, buffer_214_out);
  buf buffer_216 (buffer_216_out, buffer_215_out);
  buf buffer_217 (buffer_217_out, buffer_218_out);
  buf buffer_218 (buffer_218_out, buffer_219_out);
  buf buffer_219 (buffer_219_out, buffer_220_out);
  buf buffer_220 (buffer_220_out, buffer_237_out);
  buf buffer_221 (buffer_221_out, buffer_204_out);
  buf buffer_222 (buffer_222_out, buffer_221_out);
  buf buffer_223 (buffer_223_out, buffer_222_out);
  buf buffer_224 (buffer_224_out, buffer_223_out);
  buf buffer_225 (buffer_225_out, buffer_226_out);
  buf buffer_226 (buffer_226_out, buffer_227_out);
  buf buffer_227 (buffer_227_out, buffer_228_out);
  buf buffer_228 (buffer_228_out, buffer_245_out);
  buf buffer_229 (buffer_229_out, buffer_212_out);
  buf buffer_230 (buffer_230_out, buffer_229_out);
  buf buffer_231 (buffer_231_out, buffer_230_out);
  buf buffer_232 (buffer_232_out, buffer_231_out);
  buf buffer_233 (buffer_233_out, buffer_216_out);
  buf buffer_234 (buffer_234_out, buffer_233_out);
  buf buffer_235 (buffer_235_out, buffer_234_out);
  buf buffer_236 (buffer_236_out, buffer_235_out);
  buf buffer_237 (buffer_237_out, buffer_238_out);
  buf buffer_238 (buffer_238_out, buffer_239_out);
  buf buffer_239 (buffer_239_out, buffer_240_out);
  buf buffer_240 (buffer_240_out, buffer_257_out);
  buf buffer_241 (buffer_241_out, buffer_224_out);
  buf buffer_242 (buffer_242_out, buffer_241_out);
  buf buffer_243 (buffer_243_out, buffer_242_out);
  buf buffer_244 (buffer_244_out, buffer_243_out);
  buf buffer_245 (buffer_245_out, buffer_246_out);
  buf buffer_246 (buffer_246_out, buffer_247_out);
  buf buffer_247 (buffer_247_out, buffer_248_out);
  buf buffer_248 (buffer_248_out, buffer_265_out);
  buf buffer_249 (buffer_249_out, buffer_232_out);
  buf buffer_250 (buffer_250_out, buffer_249_out);
  buf buffer_251 (buffer_251_out, buffer_250_out);
  buf buffer_252 (buffer_252_out, buffer_251_out);
  buf buffer_253 (buffer_253_out, buffer_236_out);
  buf buffer_254 (buffer_254_out, buffer_253_out);
  buf buffer_255 (buffer_255_out, buffer_254_out);
  buf buffer_256 (buffer_256_out, buffer_255_out);
  buf buffer_257 (buffer_257_out, buffer_258_out);
  buf buffer_258 (buffer_258_out, buffer_259_out);
  buf buffer_259 (buffer_259_out, buffer_260_out);
  buf buffer_260 (buffer_260_out, buffer_277_out);
  buf buffer_261 (buffer_261_out, buffer_244_out);
  buf buffer_262 (buffer_262_out, buffer_261_out);
  buf buffer_263 (buffer_263_out, buffer_262_out);
  buf buffer_264 (buffer_264_out, buffer_263_out);
  buf buffer_265 (buffer_265_out, buffer_266_out);
  buf buffer_266 (buffer_266_out, buffer_267_out);
  buf buffer_267 (buffer_267_out, buffer_268_out);
  buf buffer_268 (buffer_268_out, buffer_285_out);
  buf buffer_269 (buffer_269_out, buffer_252_out);
  buf buffer_270 (buffer_270_out, buffer_269_out);
  buf buffer_271 (buffer_271_out, buffer_270_out);
  buf buffer_272 (buffer_272_out, buffer_271_out);
  buf buffer_273 (buffer_273_out, buffer_256_out);
  buf buffer_274 (buffer_274_out, buffer_273_out);
  buf buffer_275 (buffer_275_out, buffer_274_out);
  buf buffer_276 (buffer_276_out, buffer_275_out);
  buf buffer_277 (buffer_277_out, buffer_278_out);
  buf buffer_278 (buffer_278_out, buffer_279_out);
  buf buffer_279 (buffer_279_out, buffer_280_out);
  buf buffer_280 (buffer_280_out, buffer_297_out);
  buf buffer_281 (buffer_281_out, buffer_264_out);
  buf buffer_282 (buffer_282_out, buffer_281_out);
  buf buffer_283 (buffer_283_out, buffer_282_out);
  buf buffer_284 (buffer_284_out, buffer_283_out);
  buf buffer_285 (buffer_285_out, buffer_286_out);
  buf buffer_286 (buffer_286_out, buffer_287_out);
  buf buffer_287 (buffer_287_out, buffer_288_out);
  buf buffer_288 (buffer_288_out, buffer_304_out);
  buf buffer_289 (buffer_289_out, buffer_272_out);
  buf buffer_290 (buffer_290_out, buffer_289_out);
  buf buffer_291 (buffer_291_out, buffer_290_out);
  buf buffer_292 (buffer_292_out, buffer_291_out);
  buf buffer_293 (buffer_293_out, buffer_276_out);
  buf buffer_294 (buffer_294_out, buffer_293_out);
  buf buffer_295 (buffer_295_out, buffer_294_out);
  buf buffer_296 (buffer_296_out, buffer_295_out);
  buf buffer_297 (buffer_297_out, buffer_298_out);
  buf buffer_298 (buffer_298_out, buffer_299_out);
  buf buffer_299 (buffer_299_out, buffer_337_out);
  buf buffer_300 (buffer_300_out, buffer_284_out);
  buf buffer_301 (buffer_301_out, buffer_300_out);
  buf buffer_302 (buffer_302_out, buffer_301_out);
  buf buffer_303 (buffer_303_out, buffer_302_out);
  buf buffer_304 (buffer_304_out, buffer_305_out);
  buf buffer_305 (buffer_305_out, buffer_306_out);
  buf buffer_306 (buffer_306_out, buffer_307_out);
  buf buffer_307 (buffer_307_out, buffer_318_out);
  buf buffer_308 (buffer_308_out, buffer_292_out);
  buf buffer_309 (buffer_309_out, buffer_308_out);
  buf buffer_310 (buffer_310_out, buffer_309_out);
  buf buffer_311 (buffer_311_out, buffer_310_out);
  buf buffer_312 (buffer_312_out, buffer_296_out);
  buf buffer_313 (buffer_313_out, buffer_312_out);
  buf buffer_314 (buffer_314_out, buffer_303_out);
  buf buffer_315 (buffer_315_out, buffer_314_out);
  buf buffer_316 (buffer_316_out, buffer_315_out);
  buf buffer_317 (buffer_317_out, buffer_316_out);
  buf buffer_318 (buffer_318_out, buffer_319_out);
  buf buffer_319 (buffer_319_out, buffer_320_out);
  buf buffer_320 (buffer_320_out, buffer_321_out);
  buf buffer_321 (buffer_321_out, buffer_330_out);
  buf buffer_322 (buffer_322_out, buffer_311_out);
  buf buffer_323 (buffer_323_out, buffer_322_out);
  buf buffer_324 (buffer_324_out, buffer_323_out);
  buf buffer_325 (buffer_325_out, buffer_324_out);
  buf buffer_326 (buffer_326_out, buffer_317_out);
  buf buffer_327 (buffer_327_out, buffer_326_out);
  buf buffer_328 (buffer_328_out, buffer_327_out);
  buf buffer_329 (buffer_329_out, buffer_328_out);
  buf buffer_330 (buffer_330_out, buffer_331_out);
  buf buffer_331 (buffer_331_out, buffer_332_out);
  buf buffer_332 (buffer_332_out, buffer_341_out);
  buf buffer_333 (buffer_333_out, buffer_325_out);
  buf buffer_334 (buffer_334_out, buffer_333_out);
  buf buffer_335 (buffer_335_out, buffer_334_out);
  buf buffer_336 (buffer_336_out, buffer_335_out);
  buf buffer_337 (buffer_337_out, buffer_329_out);
  buf buffer_338 (buffer_338_out, buffer_336_out);
  buf buffer_339 (buffer_339_out, buffer_338_out);
  buf buffer_340 (buffer_340_out, buffer_339_out);
  buf buffer_341 (buffer_341_out, buffer_340_out);

  // Notes on the sheet:
  //   Multiplication takes forever :(
endmodule

module ALU_FLOAT_SECTION (
  input  [11:0] INSTRUCTION,
  input  CLK,
  input  [31:0] ALU_IN,
  output [2:0] OP_OUT,
  output ALU_SET,
  output [31:0] EF_VAL,
  output EF_SET
);

  wire buffer_1_out, buffer_2_out, buffer_3_out, buffer_4_out, buffer_5_out, buffer_6_out, buffer_7_out,
       buffer_8_out, buffer_10_out, buffer_11_out, buffer_12_out, buffer_13_out, buffer_14_out,
       buffer_15_out, buffer_16_out, buffer_17_out, buffer_18_out, buffer_19_out, buffer_20_out,
       buffer_21_out, buffer_22_out, buffer_23_out, buffer_24_out, buffer_25_out, buffer_26_out,
       buffer_27_out, buffer_28_out, buffer_29_out, buffer_30_out, buffer_31_out, buffer_32_out,
       buffer_33_out, buffer_34_out, buffer_35_out, buffer_36_out, buffer_37_out, buffer_38_out,
       buffer_39_out, buffer_40_out, buffer_41_out, buffer_42_out, buffer_43_out, buffer_44_out,
       buffer_45_out, buffer_46_out, buffer_47_out, buffer_48_out, buffer_49_out, buffer_50_out,
       buffer_51_out, buffer_52_out, buffer_53_out;

  buf buffer_1 (buffer_1_out, CLK);
  buf buffer_2 (buffer_2_out, buffer_1_out);
  buf buffer_3 (buffer_3_out, buffer_2_out);
  buf buffer_4 (buffer_4_out, buffer_3_out);
  buf buffer_5 (buffer_5_out, buffer_4_out);
  buf buffer_6 (buffer_6_out, buffer_5_out);
  Multiplexer #(.width(32)) multiplexer_1 (.in0({32{1'b0}}), .in1(ALU_IN), .out(EF_VAL), .sel(buffer_22_out));
  buf buffer_7 (buffer_7_out, buffer_22_out);
  buf buffer_8 (buffer_8_out, buffer_7_out);
  buf buffer_9 (EF_SET, buffer_8_out);
  buf buffer_10 (buffer_10_out, buffer_6_out);
  buf buffer_11 (buffer_11_out, buffer_10_out);
  buf buffer_12 (buffer_12_out, buffer_11_out);
  buf buffer_13 (buffer_13_out, buffer_12_out);
  buf buffer_14 (buffer_14_out, buffer_13_out);
  buf buffer_15 (buffer_15_out, buffer_14_out);
  buf buffer_16 (buffer_16_out, buffer_15_out);
  buf buffer_17 (buffer_17_out, buffer_16_out);
  buf buffer_18 (buffer_18_out, buffer_17_out);
  buf buffer_19 (buffer_19_out, buffer_18_out);
  buf buffer_20 (buffer_20_out, buffer_19_out);
  buf buffer_21 (buffer_21_out, buffer_20_out);
  buf buffer_22 (buffer_22_out, buffer_23_out);
  buf buffer_23 (buffer_23_out, buffer_28_out);
  buf buffer_24 (buffer_24_out, buffer_21_out);
  buf buffer_25 (buffer_25_out, buffer_24_out);
  buf buffer_26 (buffer_26_out, buffer_25_out);
  buf buffer_27 (buffer_27_out, buffer_26_out);
  buf buffer_28 (buffer_28_out, buffer_29_out);
  buf buffer_29 (buffer_29_out, buffer_30_out);
  buf buffer_30 (buffer_30_out, buffer_31_out);
  buf buffer_31 (buffer_31_out, buffer_38_out);
  buf buffer_32 (buffer_32_out, buffer_27_out);
  buf buffer_33 (buffer_33_out, buffer_32_out);
  buf buffer_34 (buffer_34_out, buffer_33_out);
  buf buffer_35 (buffer_35_out, buffer_34_out);
  buf buffer_36 (buffer_36_out, buffer_37_out);
  buf buffer_37 (buffer_37_out, buffer_44_out);
  buf buffer_38 (buffer_38_out, buffer_39_out);
  buf buffer_39 (buffer_39_out, buffer_36_out);
  buf buffer_40 (buffer_40_out, buffer_43_out);
  buf buffer_41 (buffer_41_out, buffer_40_out);
  buf buffer_42 (buffer_42_out, buffer_35_out);
  buf buffer_43 (buffer_43_out, buffer_42_out);
  buf buffer_44 (buffer_44_out, buffer_45_out);
  buf buffer_45 (buffer_45_out, buffer_46_out);
  buf buffer_46 (buffer_46_out, buffer_47_out);
  buf buffer_47 (buffer_47_out, buffer_53_out);
  buf buffer_48 (buffer_48_out, buffer_41_out);
  buf buffer_49 (buffer_49_out, buffer_48_out);
  buf buffer_50 (buffer_50_out, buffer_49_out);
  buf buffer_51 (buffer_51_out, buffer_50_out);
  buf buffer_52 (buffer_52_out, buffer_51_out);
  buf buffer_53 (buffer_53_out, buffer_52_out);

  assign ALU_SET = CLK;
  assign OP_OUT = INSTRUCTION[10:8];
endmodule

module LITERAL_JUMP_SECTION (
  input  [11:0] INSTRUCTION,
  input  CLK,
  input  [15:0] NEXT_BYTE,
  input  [7:0] CONDITIONS,
  output [15:0] JUMP_ADDR,
  output JUMP_SET
);

  wire and_1_out, and_2_out, multiplexer_1_out;

  and and_1 (and_1_out, ~INSTRUCTION[8], CLK);  // AND_Gate
  Multiplexer #(.select(3)) multiplexer_1 (
    .in0(CONDITIONS[0]), .in1(CONDITIONS[1]), .in2(CONDITIONS[2]), .in3(CONDITIONS[3]), .in4(CONDITIONS[4]),
    .in5(CONDITIONS[5]), .in6(CONDITIONS[6]), .in7(CONDITIONS[7]), .out(multiplexer_1_out),
    .sel(INSTRUCTION[6:4]));
  and and_2 (and_2_out, INSTRUCTION[8], CLK, multiplexer_1_out);
  or or_1 (JUMP_SET, and_1_out, and_2_out);

  assign JUMP_ADDR = NEXT_BYTE;
endmodule

module PrintDemo (
  input  in_1,
  input  in_2
);

  wire [3:0] cpu_1_out_clks;
  wire [15:0] cpu_1_out_0;

  CPU cpu_1 (
    .START(in_1), .RST(in_2), .OUT_0(cpu_1_out_0), .OUT_CLKS(cpu_1_out_clks));  // open: IN_0, IN_1, IN_2, IN_3, OUT_1, OUT_2, OUT_3
  TTY tty_1 (.data(cpu_1_out_0[6:0]), .clk(cpu_1_out_clks[0]), .clr(in_2));  // open: we
endmodule
